// Logisim project ALU.circ as structural Verilog
module AddSub16bit (
  input  in_1,
  input  [15:0] in_2,
  input  [15:0] in_3,
  output [15:0] out_4,
  output out_5
);

  wire and_1_out, and_2_out, and_3_out, and_4_out, and_5_out, and_6_out, and_7_out, and_8_out, and_9_out,
       and_10_out, and_11_out, and_12_out, and_13_out, and_14_out, and_15_out, and_16_out, and_17_out,
       and_18_out, and_19_out, and_20_out, and_21_out, and_22_out, and_23_out, and_24_out, and_25_out,
       and_26_out, and_27_out, and_28_out, and_29_out, and_30_out, and_31_out, and_32_out, or_1_out,
       or_2_out, or_3_out, or_4_out, or_5_out, or_6_out, or_7_out, or_8_out, or_9_out, or_10_out, or_11_out,
       or_12_out, or_13_out, or_14_out, or_15_out, xor_2_out, xor_3_out, xor_4_out, xor_5_out, xor_10_out,
       xor_11_out, xor_12_out, xor_13_out, xor_18_out, xor_19_out, xor_20_out, xor_21_out, xor_26_out,
       xor_27_out, xor_28_out, xor_29_out;
  wire [15:0] bit_extender_1_out, xor_1_out;

  assign bit_extender_1_out = {{15{in_1}}, in_1};  // Bit_Extender bit_extender_1
  assign xor_1_out = bit_extender_1_out ^ in_3;  // XOR_Gate xor_1, 16 bits wide
  xor xor_2 (xor_2_out, in_2[0], xor_1_out[0]);
  xor xor_3 (xor_3_out, in_2[4], xor_1_out[4]);
  xor xor_4 (xor_4_out, in_2[8], xor_1_out[8]);
  xor xor_5 (xor_5_out, in_2[12], xor_1_out[12]);
  xor xor_6 (out_4[0], xor_2_out, in_1);
  and and_1 (and_1_out, xor_2_out, in_1);
  and and_2 (and_2_out, in_2[0], xor_1_out[0]);
  xor xor_7 (out_4[4], xor_3_out, or_13_out);
  and and_3 (and_3_out, xor_3_out, or_13_out);
  and and_4 (and_4_out, in_2[4], xor_1_out[4]);
  xor xor_8 (out_4[8], xor_4_out, or_14_out);
  and and_5 (and_5_out, xor_4_out, or_14_out);
  and and_6 (and_6_out, in_2[8], xor_1_out[8]);
  xor xor_9 (out_4[12], xor_5_out, or_15_out);
  and and_7 (and_7_out, xor_5_out, or_15_out);
  and and_8 (and_8_out, in_2[12], xor_1_out[12]);
  or or_1 (or_1_out, and_1_out, and_2_out);
  or or_2 (or_2_out, and_3_out, and_4_out);
  or or_3 (or_3_out, and_5_out, and_6_out);
  or or_4 (or_4_out, and_7_out, and_8_out);
  xor xor_10 (xor_10_out, in_2[1], xor_1_out[1]);
  xor xor_11 (xor_11_out, in_2[5], xor_1_out[5]);
  xor xor_12 (xor_12_out, in_2[9], xor_1_out[9]);
  xor xor_13 (xor_13_out, in_2[13], xor_1_out[13]);
  xor xor_14 (out_4[1], xor_10_out, or_1_out);
  and and_9 (and_9_out, xor_10_out, or_1_out);
  and and_10 (and_10_out, in_2[1], xor_1_out[1]);
  xor xor_15 (out_4[5], xor_11_out, or_2_out);
  and and_11 (and_11_out, xor_11_out, or_2_out);
  and and_12 (and_12_out, in_2[5], xor_1_out[5]);
  xor xor_16 (out_4[9], xor_12_out, or_3_out);
  and and_13 (and_13_out, xor_12_out, or_3_out);
  and and_14 (and_14_out, in_2[9], xor_1_out[9]);
  xor xor_17 (out_4[13], xor_13_out, or_4_out);
  and and_15 (and_15_out, xor_13_out, or_4_out);
  and and_16 (and_16_out, in_2[13], xor_1_out[13]);
  or or_5 (or_5_out, and_9_out, and_10_out);
  or or_6 (or_6_out, and_11_out, and_12_out);
  or or_7 (or_7_out, and_13_out, and_14_out);
  or or_8 (or_8_out, and_15_out, and_16_out);
  xor xor_18 (xor_18_out, in_2[2], xor_1_out[2]);
  xor xor_19 (xor_19_out, in_2[6], xor_1_out[6]);
  xor xor_20 (xor_20_out, in_2[10], xor_1_out[10]);
  xor xor_21 (xor_21_out, in_2[14], xor_1_out[14]);
  xor xor_22 (out_4[2], xor_18_out, or_5_out);
  and and_17 (and_17_out, xor_18_out, or_5_out);
  and and_18 (and_18_out, in_2[2], xor_1_out[2]);
  xor xor_23 (out_4[6], xor_19_out, or_6_out);
  and and_19 (and_19_out, xor_19_out, or_6_out);
  and and_20 (and_20_out, in_2[6], xor_1_out[6]);
  xor xor_24 (out_4[10], xor_20_out, or_7_out);
  and and_21 (and_21_out, xor_20_out, or_7_out);
  and and_22 (and_22_out, in_2[10], xor_1_out[10]);
  xor xor_25 (out_4[14], xor_21_out, or_8_out);
  and and_23 (and_23_out, xor_21_out, or_8_out);
  and and_24 (and_24_out, in_2[14], xor_1_out[14]);
  or or_9 (or_9_out, and_17_out, and_18_out);
  or or_10 (or_10_out, and_19_out, and_20_out);
  or or_11 (or_11_out, and_21_out, and_22_out);
  or or_12 (or_12_out, and_23_out, and_24_out);
  xor xor_26 (xor_26_out, in_2[3], xor_1_out[3]);
  xor xor_27 (xor_27_out, in_2[7], xor_1_out[7]);
  xor xor_28 (xor_28_out, in_2[11], xor_1_out[11]);
  xor xor_29 (xor_29_out, in_2[15], xor_1_out[15]);
  xor xor_30 (out_4[3], xor_26_out, or_9_out);
  and and_25 (and_25_out, xor_26_out, or_9_out);
  and and_26 (and_26_out, in_2[3], xor_1_out[3]);
  xor xor_31 (out_4[7], xor_27_out, or_10_out);
  and and_27 (and_27_out, xor_27_out, or_10_out);
  and and_28 (and_28_out, in_2[7], xor_1_out[7]);
  xor xor_32 (out_4[11], xor_28_out, or_11_out);
  and and_29 (and_29_out, xor_28_out, or_11_out);
  and and_30 (and_30_out, in_2[11], xor_1_out[11]);
  xor xor_33 (out_4[15], xor_29_out, or_12_out);
  and and_31 (and_31_out, xor_29_out, or_12_out);
  and and_32 (and_32_out, in_2[15], xor_1_out[15]);
  or or_13 (or_13_out, and_25_out, and_26_out);
  or or_14 (or_14_out, and_27_out, and_28_out);
  or or_15 (or_15_out, and_29_out, and_30_out);
  or or_16 (out_5, and_31_out, and_32_out);
endmodule

module ALU4bit (
  input  [1:0] opCode,
  input  [3:0] A,
  input  [3:0] B,
  input  isSub,
  output [3:0] out_5,
  output [3:0] Result,
  output [3:0] out_7,
  output [3:0] out_8,
  output [3:0] out_9,
  output PG,
  output GG
);

  wire and_1_out, and_2_out, and_3_out, and_4_out, and_5_out, and_7_out, and_8_out, and_10_out, and_12_out,
       and_14_out, and_15_out, and_16_out, and_17_out, and_18_out, and_19_out, and_20_out, and_21_out,
       not_1_out, not_2_out, not_3_out, not_4_out, or_2_out, or_3_out, or_4_out, xor_3_out, xor_4_out,
       xor_5_out, xor_6_out;
  wire [3:0] and_6_out, and_23_out, bit_extender_1_out, bit_extender_2_out, bit_extender_3_out,
       bit_extender_4_out, bit_extender_5_out, or_1_out, xor_1_out, xor_2_out;

  assign bit_extender_1_out = {{3{isSub}}, isSub};  // Bit_Extender bit_extender_1
  assign xor_1_out = B ^ bit_extender_1_out;  // XOR_Gate xor_1, 4 bits wide
  assign xor_2_out = A ^ B;  // XOR_Gate xor_2, 4 bits wide
  xor xor_3 (xor_3_out, xor_1_out[0], A[0]);
  and and_1 (and_1_out, A[0], xor_1_out[0]);
  xor xor_4 (xor_4_out, xor_1_out[1], A[1]);
  and and_2 (and_2_out, A[1], xor_1_out[1]);
  xor xor_5 (xor_5_out, xor_1_out[2], A[2]);
  and and_3 (and_3_out, A[2], xor_1_out[2]);
  xor xor_6 (xor_6_out, xor_1_out[3], A[3]);
  and and_4 (and_4_out, A[3], xor_1_out[3]);
  assign or_1_out = A | B;  // OR_Gate or_1, 4 bits wide
  xor xor_7 (out_8[0], isSub, xor_3_out);
  xor xor_8 (out_8[1], or_2_out, xor_4_out);
  xor xor_9 (out_8[2], or_3_out, xor_5_out);
  xor xor_10 (out_8[3], or_4_out, xor_6_out);
  and and_5 (and_5_out, opCode[1], opCode[0]);
  assign and_6_out = A & B;  // AND_Gate and_6, 4 bits wide
  or or_2 (or_2_out, and_1_out, and_14_out);
  or or_3 (or_3_out, and_2_out, and_15_out, and_16_out);
  or or_4 (or_4_out, and_3_out, and_17_out, and_18_out, and_10_out);
  or or_5 (GG, and_4_out, and_19_out, and_20_out, and_21_out);
  not not_1 (not_1_out, opCode[1]);
  not not_2 (not_2_out, opCode[0]);
  and and_7 (and_7_out, not_1_out, opCode[0]);
  and and_8 (and_8_out, opCode[1], not_2_out);
  assign bit_extender_2_out = {{3{and_7_out}}, and_7_out};  // Bit_Extender bit_extender_2
  assign bit_extender_3_out = {{3{and_5_out}}, and_5_out};  // Bit_Extender bit_extender_3
  assign out_9 = bit_extender_3_out & xor_2_out;  // AND_Gate and_9, 4 bits wide
  and and_10 (and_10_out, xor_5_out, xor_4_out, xor_3_out, isSub);
  and and_11 (PG, xor_6_out, xor_5_out, xor_4_out, xor_3_out);
  not not_3 (not_3_out, opCode[1]);
  not not_4 (not_4_out, opCode[0]);
  and and_12 (and_12_out, not_3_out, not_4_out);
  assign bit_extender_4_out = {{3{and_8_out}}, and_8_out};  // Bit_Extender bit_extender_4
  assign out_7 = bit_extender_2_out & or_1_out;  // AND_Gate and_13, 4 bits wide
  and and_14 (and_14_out, isSub, xor_3_out);
  and and_15 (and_15_out, xor_4_out, and_1_out);
  and and_16 (and_16_out, xor_4_out, xor_3_out, isSub);
  and and_17 (and_17_out, xor_5_out, and_2_out);
  and and_18 (and_18_out, xor_5_out, xor_4_out, and_1_out);
  and and_19 (and_19_out, xor_6_out, and_3_out);
  and and_20 (and_20_out, xor_6_out, xor_5_out, and_2_out);
  and and_21 (and_21_out, xor_6_out, xor_5_out, xor_4_out, and_1_out);
  assign bit_extender_5_out = {{3{and_12_out}}, and_12_out};  // Bit_Extender bit_extender_5
  assign out_5 = bit_extender_4_out & and_6_out;  // AND_Gate and_22, 4 bits wide
  assign and_23_out = bit_extender_5_out & out_8;  // AND_Gate and_23, 4 bits wide
  assign Result = out_5 | out_7 | out_9 | and_23_out;  // OR_Gate or_6, 4 bits wide
endmodule
