// Logisim project Eclipse-10000.circ as structural Verilog
module ignote (
  input  in_1,
  input  [15:0] in_2,
  input  [15:0] in_3,
  output [15:0] out_4,
  output out_5
);

  wire and_1_out, and_2_out, and_3_out, and_4_out, and_5_out, and_6_out, and_7_out, and_8_out, and_9_out,
       and_10_out, and_11_out, and_12_out, and_13_out, and_14_out, and_15_out, and_16_out, and_17_out,
       and_18_out, and_19_out, and_20_out, and_21_out, and_22_out, and_23_out, and_24_out, and_25_out,
       and_26_out, and_27_out, and_28_out, and_29_out, and_30_out, and_31_out, and_32_out, or_1_out,
       or_2_out, or_3_out, or_4_out, or_5_out, or_6_out, or_7_out, or_8_out, or_9_out, or_10_out, or_11_out,
       or_12_out, or_13_out, or_14_out, or_15_out, xor_2_out, xor_3_out, xor_4_out, xor_5_out, xor_10_out,
       xor_11_out, xor_12_out, xor_13_out, xor_18_out, xor_19_out, xor_20_out, xor_21_out, xor_26_out,
       xor_27_out, xor_28_out, xor_29_out;
  wire [15:0] bit_extender_1_out, xor_1_out;

  assign bit_extender_1_out = {{15{in_1}}, in_1};  // Bit_Extender bit_extender_1
  assign xor_1_out = bit_extender_1_out ^ in_3;  // XOR_Gate xor_1, 16 bits wide
  xor xor_2 (xor_2_out, in_2[0], xor_1_out[0]);
  xor xor_3 (xor_3_out, in_2[4], xor_1_out[4]);
  xor xor_4 (xor_4_out, in_2[8], xor_1_out[8]);
  xor xor_5 (xor_5_out, in_2[12], xor_1_out[12]);
  xor xor_6 (out_4[0], xor_2_out, in_1);
  and and_1 (and_1_out, xor_2_out, in_1);
  and and_2 (and_2_out, in_2[0], xor_1_out[0]);
  xor xor_7 (out_4[4], xor_3_out, or_13_out);
  and and_3 (and_3_out, xor_3_out, or_13_out);
  and and_4 (and_4_out, in_2[4], xor_1_out[4]);
  xor xor_8 (out_4[8], xor_4_out, or_14_out);
  and and_5 (and_5_out, xor_4_out, or_14_out);
  and and_6 (and_6_out, in_2[8], xor_1_out[8]);
  xor xor_9 (out_4[12], xor_5_out, or_15_out);
  and and_7 (and_7_out, xor_5_out, or_15_out);
  and and_8 (and_8_out, in_2[12], xor_1_out[12]);
  or or_1 (or_1_out, and_1_out, and_2_out);
  or or_2 (or_2_out, and_3_out, and_4_out);
  or or_3 (or_3_out, and_5_out, and_6_out);
  or or_4 (or_4_out, and_7_out, and_8_out);
  xor xor_10 (xor_10_out, in_2[1], xor_1_out[1]);
  xor xor_11 (xor_11_out, in_2[5], xor_1_out[5]);
  xor xor_12 (xor_12_out, in_2[9], xor_1_out[9]);
  xor xor_13 (xor_13_out, in_2[13], xor_1_out[13]);
  xor xor_14 (out_4[1], xor_10_out, or_1_out);
  and and_9 (and_9_out, xor_10_out, or_1_out);
  and and_10 (and_10_out, in_2[1], xor_1_out[1]);
  xor xor_15 (out_4[5], xor_11_out, or_2_out);
  and and_11 (and_11_out, xor_11_out, or_2_out);
  and and_12 (and_12_out, in_2[5], xor_1_out[5]);
  xor xor_16 (out_4[9], xor_12_out, or_3_out);
  and and_13 (and_13_out, xor_12_out, or_3_out);
  and and_14 (and_14_out, in_2[9], xor_1_out[9]);
  xor xor_17 (out_4[13], xor_13_out, or_4_out);
  and and_15 (and_15_out, xor_13_out, or_4_out);
  and and_16 (and_16_out, in_2[13], xor_1_out[13]);
  or or_5 (or_5_out, and_9_out, and_10_out);
  or or_6 (or_6_out, and_11_out, and_12_out);
  or or_7 (or_7_out, and_13_out, and_14_out);
  or or_8 (or_8_out, and_15_out, and_16_out);
  xor xor_18 (xor_18_out, in_2[2], xor_1_out[2]);
  xor xor_19 (xor_19_out, in_2[6], xor_1_out[6]);
  xor xor_20 (xor_20_out, in_2[10], xor_1_out[10]);
  xor xor_21 (xor_21_out, in_2[14], xor_1_out[14]);
  xor xor_22 (out_4[2], xor_18_out, or_5_out);
  and and_17 (and_17_out, xor_18_out, or_5_out);
  and and_18 (and_18_out, in_2[2], xor_1_out[2]);
  xor xor_23 (out_4[6], xor_19_out, or_6_out);
  and and_19 (and_19_out, xor_19_out, or_6_out);
  and and_20 (and_20_out, in_2[6], xor_1_out[6]);
  xor xor_24 (out_4[10], xor_20_out, or_7_out);
  and and_21 (and_21_out, xor_20_out, or_7_out);
  and and_22 (and_22_out, in_2[10], xor_1_out[10]);
  xor xor_25 (out_4[14], xor_21_out, or_8_out);
  and and_23 (and_23_out, xor_21_out, or_8_out);
  and and_24 (and_24_out, in_2[14], xor_1_out[14]);
  or or_9 (or_9_out, and_17_out, and_18_out);
  or or_10 (or_10_out, and_19_out, and_20_out);
  or or_11 (or_11_out, and_21_out, and_22_out);
  or or_12 (or_12_out, and_23_out, and_24_out);
  xor xor_26 (xor_26_out, in_2[3], xor_1_out[3]);
  xor xor_27 (xor_27_out, in_2[7], xor_1_out[7]);
  xor xor_28 (xor_28_out, in_2[11], xor_1_out[11]);
  xor xor_29 (xor_29_out, in_2[15], xor_1_out[15]);
  xor xor_30 (out_4[3], xor_26_out, or_9_out);
  and and_25 (and_25_out, xor_26_out, or_9_out);
  and and_26 (and_26_out, in_2[3], xor_1_out[3]);
  xor xor_31 (out_4[7], xor_27_out, or_10_out);
  and and_27 (and_27_out, xor_27_out, or_10_out);
  and and_28 (and_28_out, in_2[7], xor_1_out[7]);
  xor xor_32 (out_4[11], xor_28_out, or_11_out);
  and and_29 (and_29_out, xor_28_out, or_11_out);
  and and_30 (and_30_out, in_2[11], xor_1_out[11]);
  xor xor_33 (out_4[15], xor_29_out, or_12_out);
  and and_31 (and_31_out, xor_29_out, or_12_out);
  and and_32 (and_32_out, in_2[15], xor_1_out[15]);
  or or_13 (or_13_out, and_25_out, and_26_out);
  or or_14 (or_14_out, and_27_out, and_28_out);
  or or_15 (or_15_out, and_29_out, and_30_out);
  or or_16 (out_5, and_31_out, and_32_out);
endmodule

module CLA4bit (
  input  [3:0] X,
  input  [3:0] Y,
  input  isSub,
  input  Cin,
  output [3:0] Result,
  output PG,
  output GG
);

  wire and_1_out, and_2_out, and_3_out, and_4_out, and_6_out, and_7_out, and_8_out, and_9_out, and_10_out,
       and_11_out, and_12_out, and_13_out, and_14_out, or_1_out, or_3_out, or_4_out, xor_2_out, xor_3_out,
       xor_4_out, xor_5_out;
  wire [3:0] bit_extender_1_out, xor_1_out;

  assign bit_extender_1_out = {{3{isSub}}, isSub};  // Bit_Extender bit_extender_1
  assign xor_1_out = Y ^ bit_extender_1_out;  // XOR_Gate xor_1, 4 bits wide
  xor xor_2 (xor_2_out, xor_1_out[0], X[0]);
  and and_1 (and_1_out, X[0], xor_1_out[0]);
  xor xor_3 (xor_3_out, xor_1_out[1], X[1]);
  and and_2 (and_2_out, X[1], xor_1_out[1]);
  xor xor_4 (xor_4_out, xor_1_out[2], X[2]);
  and and_3 (and_3_out, X[2], xor_1_out[2]);
  xor xor_5 (xor_5_out, xor_1_out[3], X[3]);
  and and_4 (and_4_out, X[3], xor_1_out[3]);
  xor xor_6 (Result[0], Cin, xor_2_out);
  xor xor_7 (Result[1], or_1_out, xor_3_out);
  xor xor_8 (Result[2], or_3_out, xor_4_out);
  xor xor_9 (Result[3], or_4_out, xor_5_out);
  or or_1 (or_1_out, and_1_out, and_12_out);
  or or_2 (GG, and_4_out, and_9_out, and_10_out, and_11_out);
  or or_3 (or_3_out, and_2_out, and_6_out, and_7_out);
  or or_4 (or_4_out, and_3_out, and_13_out, and_14_out, and_8_out);
  and and_5 (PG, xor_5_out, xor_4_out, xor_3_out, xor_2_out);
  and and_6 (and_6_out, xor_3_out, and_1_out);
  and and_7 (and_7_out, xor_3_out, xor_2_out, Cin);
  and and_8 (and_8_out, xor_4_out, xor_3_out, xor_2_out, Cin);
  and and_9 (and_9_out, xor_5_out, and_3_out);
  and and_10 (and_10_out, xor_5_out, xor_4_out, and_2_out);
  and and_11 (and_11_out, xor_5_out, xor_4_out, xor_3_out, and_1_out);
  and and_12 (and_12_out, Cin, xor_2_out);
  and and_13 (and_13_out, xor_4_out, and_2_out);
  and and_14 (and_14_out, xor_4_out, xor_3_out, and_1_out);
endmodule

module ALU (
  input  [15:0] X,
  input  [15:0] Y,
  input  [3:0] opcode,
  input  [4:0] Shift,
  output [15:0] Result,
  output OverflowFlag,
  output ZeroFlag,
  output NegativeFlag,
  output [15:0] ResultRx1
);

  wire decoder4_16_1_sub_0100, nor_1_out, not_1_out;
  wire [15:0] and_1_out, and_2_out, and_3_out, and_4_out, and_5_out, and_6_out, and_7_out, and_9_out,
       and_10_out, and_11_out, bit_extender_1_out, cla16bit_1_result, cla16bit_2_result,
       decoder4_16_1_add_0000, decoder4_16_1_and_0010, decoder4_16_1_not_0101, decoder4_16_1_or_0001,
       decoder4_16_1_shl_1000, decoder4_16_1_shr_1100, decoder4_16_1_xor_0011, not_2_out, or_1_out,
       shl_1_resutl, shr_1_resutl, xor_1_out;
  wire [31:0] decoder4_16_1_mul_1111, wt16bit_1_out_3;

  Decoder4_16 decoder4_16_1 (
    .opcode(opcode), .Add_0000(decoder4_16_1_add_0000), .Sub_0100(decoder4_16_1_sub_0100),
    .XOR_0011(decoder4_16_1_xor_0011), .OR_0001(decoder4_16_1_or_0001), .AND_0010(decoder4_16_1_and_0010),
    .NOT_0101(decoder4_16_1_not_0101), .SHL_1000(decoder4_16_1_shl_1000), .SHR_1100(decoder4_16_1_shr_1100),
    .MUL_1111(decoder4_16_1_mul_1111));  // open: out_11, out_12, out_13, out_14, out_15, out_16
  CLA16bit cla16bit_1 (.X(X), .Y(Y), .Result(cla16bit_1_result));  // open: isSub, Cin, OverflowFlag
  assign and_1_out = decoder4_16_1_add_0000 & cla16bit_1_result;  // AND_Gate and_1, 16 bits wide
  CLA16bit cla16bit_2 (
    .X(X), .Y(Y), .isSub(decoder4_16_1_sub_0100), .Result(cla16bit_2_result), .OverflowFlag(OverflowFlag));  // open: Cin
  assign bit_extender_1_out = {{15{decoder4_16_1_sub_0100}}, decoder4_16_1_sub_0100};  // Bit_Extender bit_extender_1
  assign and_2_out = bit_extender_1_out & cla16bit_2_result;  // AND_Gate and_2, 16 bits wide
  assign or_1_out = Y | X;  // OR_Gate or_1, 16 bits wide
  assign xor_1_out = Y ^ X;  // XOR_Gate xor_1, 16 bits wide
  assign and_3_out = decoder4_16_1_xor_0011 & xor_1_out;  // AND_Gate and_3, 16 bits wide
  assign and_4_out = decoder4_16_1_or_0001 & or_1_out;  // AND_Gate and_4, 16 bits wide
  assign {NegativeFlag, Result[14:0]} = and_2_out | and_1_out | and_3_out | and_4_out | and_6_out | and_7_out | and_9_out | and_10_out | and_11_out;  // OR_Gate or_2, 16 bits wide
  assign and_5_out = Y & X;  // AND_Gate and_5, 16 bits wide
  assign and_6_out = decoder4_16_1_and_0010 & and_5_out;  // AND_Gate and_6, 16 bits wide
  nor nor_1 (nor_1_out, Result[0], Result[1], Result[2], Result[3], Result[4], Result[5], Result[6], Result[7], Result[8], Result[9], Result[10], Result[11], Result[12], Result[13], Result[14]);
  not not_1 (not_1_out, NegativeFlag);
  assign not_2_out = ~X;  // NOT_Gate not_2, 16 bits wide
  assign and_7_out = decoder4_16_1_not_0101 & not_2_out;  // AND_Gate and_7, 16 bits wide
  and and_8 (ZeroFlag, nor_1_out, not_1_out);
  SHL shl_1 (.X(X), .Shift(Shift), .Pad(1'b0), .Resutl(shl_1_resutl));
  assign and_9_out = decoder4_16_1_shl_1000 & shl_1_resutl;  // AND_Gate and_9, 16 bits wide
  assign and_10_out = decoder4_16_1_shr_1100 & shr_1_resutl;  // AND_Gate and_10, 16 bits wide
  SHR shr_1 (.X(X), .Shift(Shift), .Pad(1'b0), .Resutl(shr_1_resutl));
  WT16bit wt16bit_1 (.X(Y), .Y(X), .out_3(wt16bit_1_out_3));
  assign {ResultRx1, and_11_out} = decoder4_16_1_mul_1111 & wt16bit_1_out_3;  // AND_Gate and_11, 32 bits wide

  assign Result[15] = NegativeFlag;
endmodule

module Decoder4_16 (
  input  [3:0] opcode,
  output [15:0] Add_0000,
  output Sub_0100,
  output [15:0] XOR_0011,
  output [15:0] OR_0001,
  output [15:0] AND_0010,
  output [15:0] NOT_0101,
  output [15:0] SHL_1000,
  output [15:0] SHR_1100,
  output [31:0] MUL_1111,
  output out_11,
  output out_12,
  output out_13,
  output out_14,
  output out_15,
  output out_16
);

  wire and_1_out, and_3_out, and_4_out, and_5_out, and_6_out, and_7_out, and_8_out, and_9_out, and_16_out,
       not_1_out, not_2_out, not_3_out, not_4_out, not_5_out, not_6_out, not_7_out, not_8_out, not_9_out,
       not_10_out, not_11_out, not_12_out, not_13_out, not_14_out, not_15_out, not_16_out, not_17_out,
       not_18_out, not_19_out, not_20_out, not_21_out, not_22_out, not_23_out, not_24_out, not_25_out,
       not_26_out, not_27_out, not_28_out, not_29_out, not_30_out;

  not not_1 (not_1_out, opcode[0]);
  and and_1 (and_1_out, not_1_out, opcode[1], not_2_out, not_3_out);
  not not_2 (not_2_out, opcode[2]);
  not not_3 (not_3_out, opcode[3]);
  not not_4 (not_4_out, opcode[0]);
  not not_5 (not_5_out, opcode[1]);
  and and_2 (Sub_0100, not_4_out, not_5_out, opcode[2], not_6_out);
  not not_6 (not_6_out, opcode[3]);
  and and_3 (and_3_out, opcode[0], opcode[1], not_7_out, not_8_out);
  not not_7 (not_7_out, opcode[2]);
  not not_8 (not_8_out, opcode[3]);
  not not_9 (not_9_out, opcode[1]);
  and and_4 (and_4_out, opcode[0], not_9_out, not_10_out, not_11_out);
  not not_10 (not_10_out, opcode[2]);
  not not_11 (not_11_out, opcode[3]);
  not not_12 (not_12_out, opcode[0]);
  not not_13 (not_13_out, opcode[1]);
  and and_5 (and_5_out, not_12_out, not_13_out, not_14_out, not_15_out);
  not not_14 (not_14_out, opcode[2]);
  not not_15 (not_15_out, opcode[3]);
  not not_16 (not_16_out, opcode[1]);
  and and_6 (and_6_out, opcode[0], not_16_out, opcode[2], not_17_out);
  not not_17 (not_17_out, opcode[3]);
  not not_18 (not_18_out, opcode[0]);
  not not_19 (not_19_out, opcode[1]);
  and and_7 (and_7_out, not_18_out, not_19_out, not_20_out, opcode[3]);
  not not_20 (not_20_out, opcode[2]);
  not not_21 (not_21_out, opcode[0]);
  not not_22 (not_22_out, opcode[1]);
  and and_8 (and_8_out, not_21_out, not_22_out, opcode[2], opcode[3]);
  and and_9 (and_9_out, opcode[0], opcode[1], opcode[2], opcode[3]);
  and and_10 (out_11, opcode[0], opcode[1], not_23_out, opcode[3]);
  not not_23 (not_23_out, opcode[2]);
  not not_24 (not_24_out, opcode[0]);
  and and_11 (out_12, not_24_out, opcode[1], not_25_out, opcode[3]);
  not not_25 (not_25_out, opcode[2]);
  not not_26 (not_26_out, opcode[0]);
  and and_12 (out_13, not_26_out, opcode[1], opcode[2], opcode[3]);
  not not_27 (not_27_out, opcode[1]);
  and and_13 (out_14, opcode[0], not_27_out, opcode[2], opcode[3]);
  not not_28 (not_28_out, opcode[0]);
  and and_14 (out_15, not_28_out, opcode[1], not_29_out, opcode[3]);
  not not_29 (not_29_out, opcode[2]);
  and and_15 (out_16, opcode[0], opcode[1], opcode[2], not_30_out);
  not not_30 (not_30_out, opcode[3]);
  and and_16 (and_16_out, opcode[0], opcode[1], opcode[2], opcode[3]);
  assign Add_0000 = {{15{and_1_out}}, and_1_out};  // Bit_Extender bit_extender_1
  assign XOR_0011 = {{15{and_3_out}}, and_3_out};  // Bit_Extender bit_extender_2
  assign OR_0001 = {{15{and_4_out}}, and_4_out};  // Bit_Extender bit_extender_3
  assign AND_0010 = {{15{and_5_out}}, and_5_out};  // Bit_Extender bit_extender_4
  assign NOT_0101 = {{15{and_6_out}}, and_6_out};  // Bit_Extender bit_extender_5
  assign SHL_1000 = {{15{and_7_out}}, and_7_out};  // Bit_Extender bit_extender_6
  assign SHR_1100 = {{15{and_8_out}}, and_8_out};  // Bit_Extender bit_extender_7
  assign MUL_1111 = {{31{and_9_out}}, and_9_out};  // Bit_Extender bit_extender_8
endmodule

module CLA16bit (
  input  [15:0] X,
  input  [15:0] Y,
  input  isSub,
  input  Cin,
  output [15:0] Result,
  output OverflowFlag
);

  wire and_1_out, and_2_out, and_3_out, and_4_out, and_5_out, and_6_out, and_7_out, and_8_out, and_9_out,
       and_10_out, and_11_out, and_12_out, cla4bit_1_gg, cla4bit_1_pg, cla4bit_2_gg, cla4bit_2_pg,
       cla4bit_3_gg, cla4bit_3_pg, cla4bit_4_gg, cla4bit_4_pg, not_1_out, not_2_out, not_3_out, or_2_out,
       or_3_out, or_4_out, or_5_out, or_6_out;

  not not_1 (not_1_out, X[15]);
  not not_2 (not_2_out, Result[15]);
  not not_3 (not_3_out, X[15]);
  and and_1 (and_1_out, X[15], not_1_out, not_2_out);
  and and_2 (and_2_out, not_3_out, Y[15], Result[15]);
  or or_1 (OverflowFlag, and_1_out, and_2_out);
  or or_2 (or_2_out, isSub, Cin);
  // XOR_Gate xor_1 has open pins: in0=or_2_out, in1=or_4_out, out=open
  CLA4bit cla4bit_1 (
    .X(X[3:0]), .Y(Y[3:0]), .isSub(or_2_out), .Cin(or_2_out), .Result(Result[3:0]), .PG(cla4bit_1_pg),
    .GG(cla4bit_1_gg));
  CLA4bit cla4bit_2 (
    .X(X[7:4]), .Y(Y[7:4]), .isSub(or_2_out), .Cin(or_5_out), .Result(Result[7:4]), .PG(cla4bit_2_pg),
    .GG(cla4bit_2_gg));
  CLA4bit cla4bit_3 (
    .X(X[11:8]), .Y(Y[11:8]), .isSub(or_2_out), .Cin(or_6_out), .Result(Result[11:8]), .PG(cla4bit_3_pg),
    .GG(cla4bit_3_gg));
  or or_3 (or_3_out, cla4bit_3_gg, and_3_out, and_4_out, and_5_out);
  CLA4bit cla4bit_4 (
    .X(X[15:12]), .Y(Y[15:12]), .isSub(or_2_out), .Cin(or_3_out), .Result(Result[15:12]), .PG(cla4bit_4_pg),
    .GG(cla4bit_4_gg));
  or or_4 (or_4_out, cla4bit_4_gg, and_6_out, and_7_out, and_8_out, and_9_out);
  or or_5 (or_5_out, cla4bit_1_gg, and_10_out);
  or or_6 (or_6_out, cla4bit_2_gg, and_11_out, and_12_out);
  and and_3 (and_3_out, cla4bit_3_pg, cla4bit_2_gg);
  and and_4 (and_4_out, cla4bit_1_gg, cla4bit_2_pg, cla4bit_3_pg);
  and and_5 (and_5_out, cla4bit_3_pg, cla4bit_2_pg, cla4bit_1_pg, or_2_out);
  and and_6 (and_6_out, cla4bit_3_gg, cla4bit_4_pg);
  and and_7 (and_7_out, cla4bit_2_gg, cla4bit_3_pg, cla4bit_4_pg);
  and and_8 (and_8_out, cla4bit_4_pg, cla4bit_2_pg, cla4bit_1_gg, cla4bit_3_pg);
  and and_9 (and_9_out, cla4bit_4_pg, cla4bit_3_pg, cla4bit_2_pg, cla4bit_1_pg, or_2_out);
  and and_10 (and_10_out, or_2_out, cla4bit_1_pg);
  and and_11 (and_11_out, cla4bit_1_gg, cla4bit_2_pg);
  and and_12 (and_12_out, cla4bit_2_pg, cla4bit_1_pg, or_2_out);
endmodule

module SHR (
  input  [15:0] X,
  input  [4:0] Shift,
  input  Pad,
  output [15:0] Resutl
);

  wire and_1_out, and_2_out, and_3_out, and_4_out, and_5_out, and_6_out, and_7_out, and_8_out, and_9_out,
       and_10_out, and_11_out, and_12_out, and_13_out, and_14_out, and_15_out, and_16_out, and_17_out,
       and_18_out, and_19_out, and_20_out, and_21_out, and_22_out, and_23_out, and_24_out, and_25_out,
       and_26_out, and_27_out, and_28_out, and_29_out, and_30_out, and_31_out, and_32_out, and_33_out,
       and_34_out, and_35_out, and_36_out, and_37_out, and_38_out, and_39_out, and_40_out, and_41_out,
       and_42_out, and_43_out, and_44_out, and_45_out, and_46_out, and_47_out, and_48_out, and_49_out,
       and_50_out, and_51_out, and_52_out, and_53_out, and_54_out, and_55_out, and_56_out, and_57_out,
       and_58_out, and_59_out, and_60_out, and_61_out, and_62_out, and_63_out, and_64_out, and_65_out,
       and_66_out, and_67_out, and_68_out, and_69_out, and_70_out, and_71_out, and_72_out, and_73_out,
       and_74_out, and_75_out, and_76_out, and_77_out, and_78_out, and_79_out, and_80_out, and_81_out,
       and_82_out, and_83_out, and_84_out, and_85_out, and_86_out, and_87_out, and_88_out, and_89_out,
       and_90_out, and_91_out, and_92_out, and_93_out, and_94_out, and_95_out, and_96_out, and_97_out,
       and_98_out, and_99_out, and_100_out, and_101_out, and_102_out, and_103_out, and_104_out, and_105_out,
       and_106_out, and_107_out, and_108_out, and_109_out, and_110_out, and_111_out, and_112_out,
       and_113_out, and_114_out, and_115_out, and_116_out, and_117_out, and_118_out, and_119_out,
       and_120_out, and_121_out, and_122_out, and_123_out, and_124_out, and_125_out, and_126_out,
       and_127_out, and_128_out, not_1_out, not_2_out, not_3_out, not_4_out, not_5_out, not_6_out, not_7_out,
       not_8_out, not_9_out, not_10_out, not_11_out, not_12_out, not_13_out, not_14_out, not_15_out,
       not_16_out, not_17_out, not_18_out, not_19_out, not_20_out, not_21_out, not_22_out, not_23_out,
       not_24_out, not_25_out, not_26_out, not_27_out, not_28_out, not_29_out, not_30_out, not_31_out,
       not_32_out, not_33_out, not_34_out, not_35_out, not_36_out, not_37_out, not_38_out, not_39_out,
       not_40_out, not_41_out, not_42_out, not_43_out, not_44_out, not_45_out, not_46_out, not_47_out,
       not_48_out, not_49_out, not_50_out, not_51_out, not_52_out, not_53_out, not_54_out, not_55_out,
       not_56_out, not_57_out, not_58_out, not_59_out, not_60_out, not_61_out, not_62_out, not_63_out,
       not_64_out, or_1_out, or_2_out, or_3_out, or_4_out, or_5_out, or_6_out, or_7_out, or_8_out, or_9_out,
       or_10_out, or_11_out, or_12_out, or_13_out, or_14_out, or_15_out, or_16_out, or_17_out, or_18_out,
       or_19_out, or_20_out, or_21_out, or_22_out, or_23_out, or_24_out, or_25_out, or_26_out, or_27_out,
       or_28_out, or_29_out, or_30_out, or_31_out, or_32_out, or_33_out, or_34_out, or_35_out, or_36_out,
       or_37_out, or_38_out, or_39_out, or_40_out, or_41_out, or_42_out, or_43_out, or_44_out, or_45_out,
       or_46_out, or_47_out, or_48_out;

  not not_1 (not_1_out, Shift[0]);
  not not_2 (not_2_out, Shift[0]);
  not not_3 (not_3_out, Shift[0]);
  not not_4 (not_4_out, Shift[0]);
  not not_5 (not_5_out, Shift[0]);
  not not_6 (not_6_out, Shift[0]);
  not not_7 (not_7_out, Shift[0]);
  not not_8 (not_8_out, Shift[0]);
  not not_9 (not_9_out, Shift[0]);
  not not_10 (not_10_out, Shift[0]);
  not not_11 (not_11_out, Shift[0]);
  not not_12 (not_12_out, Shift[0]);
  not not_13 (not_13_out, Shift[0]);
  not not_14 (not_14_out, Shift[0]);
  not not_15 (not_15_out, Shift[0]);
  not not_16 (not_16_out, Shift[0]);
  and and_1 (and_1_out, not_1_out, X[0]);
  or or_1 (or_1_out, and_1_out, and_2_out);
  and and_2 (and_2_out, Shift[0], X[1]);
  and and_3 (and_3_out, not_2_out, X[1]);
  or or_2 (or_2_out, and_3_out, and_4_out);
  and and_4 (and_4_out, Shift[0], X[2]);
  and and_5 (and_5_out, not_3_out, X[2]);
  or or_3 (or_3_out, and_5_out, and_6_out);
  and and_6 (and_6_out, Shift[0], X[3]);
  and and_7 (and_7_out, not_4_out, X[3]);
  or or_4 (or_4_out, and_7_out, and_8_out);
  and and_8 (and_8_out, Shift[0], X[4]);
  and and_9 (and_9_out, not_5_out, X[4]);
  or or_5 (or_5_out, and_9_out, and_10_out);
  and and_10 (and_10_out, Shift[0], X[5]);
  and and_11 (and_11_out, not_6_out, X[5]);
  or or_6 (or_6_out, and_11_out, and_12_out);
  and and_12 (and_12_out, Shift[0], X[6]);
  and and_13 (and_13_out, not_7_out, X[6]);
  or or_7 (or_7_out, and_13_out, and_14_out);
  and and_14 (and_14_out, Shift[0], X[7]);
  and and_15 (and_15_out, not_8_out, X[7]);
  or or_8 (or_8_out, and_15_out, and_16_out);
  and and_16 (and_16_out, Shift[0], X[8]);
  and and_17 (and_17_out, not_9_out, X[8]);
  or or_9 (or_9_out, and_17_out, and_18_out);
  and and_18 (and_18_out, Shift[0], X[9]);
  and and_19 (and_19_out, not_10_out, X[9]);
  or or_10 (or_10_out, and_19_out, and_20_out);
  and and_20 (and_20_out, Shift[0], X[10]);
  and and_21 (and_21_out, not_11_out, X[10]);
  or or_11 (or_11_out, and_21_out, and_22_out);
  and and_22 (and_22_out, Shift[0], X[11]);
  and and_23 (and_23_out, not_12_out, X[11]);
  or or_12 (or_12_out, and_23_out, and_24_out);
  and and_24 (and_24_out, Shift[0], X[12]);
  and and_25 (and_25_out, not_13_out, X[12]);
  or or_13 (or_13_out, and_25_out, and_26_out);
  and and_26 (and_26_out, Shift[0], X[13]);
  and and_27 (and_27_out, not_14_out, X[13]);
  or or_14 (or_14_out, and_27_out, and_28_out);
  and and_28 (and_28_out, Shift[0], X[14]);
  and and_29 (and_29_out, not_15_out, X[14]);
  or or_15 (or_15_out, and_29_out, and_30_out);
  and and_30 (and_30_out, Shift[0], X[15]);
  and and_31 (and_31_out, not_16_out, X[15]);
  or or_16 (or_16_out, and_31_out, and_32_out);
  and and_32 (and_32_out, Shift[0], Pad);
  not not_17 (not_17_out, Shift[1]);
  and and_33 (and_33_out, not_17_out, or_1_out);
  and and_34 (and_34_out, Shift[1], or_3_out);
  not not_18 (not_18_out, Shift[1]);
  and and_35 (and_35_out, not_18_out, or_2_out);
  and and_36 (and_36_out, Shift[1], or_4_out);
  not not_19 (not_19_out, Shift[1]);
  and and_37 (and_37_out, not_19_out, or_3_out);
  and and_38 (and_38_out, Shift[1], or_5_out);
  not not_20 (not_20_out, Shift[1]);
  and and_39 (and_39_out, not_20_out, or_4_out);
  and and_40 (and_40_out, Shift[1], or_6_out);
  not not_21 (not_21_out, Shift[1]);
  and and_41 (and_41_out, not_21_out, or_5_out);
  and and_42 (and_42_out, Shift[1], or_7_out);
  not not_22 (not_22_out, Shift[1]);
  and and_43 (and_43_out, not_22_out, or_6_out);
  and and_44 (and_44_out, Shift[1], or_8_out);
  not not_23 (not_23_out, Shift[1]);
  and and_45 (and_45_out, not_23_out, or_7_out);
  and and_46 (and_46_out, Shift[1], or_9_out);
  not not_24 (not_24_out, Shift[1]);
  and and_47 (and_47_out, not_24_out, or_8_out);
  and and_48 (and_48_out, Shift[1], or_10_out);
  not not_25 (not_25_out, Shift[1]);
  and and_49 (and_49_out, not_25_out, or_9_out);
  and and_50 (and_50_out, Shift[1], or_11_out);
  not not_26 (not_26_out, Shift[1]);
  and and_51 (and_51_out, not_26_out, or_10_out);
  and and_52 (and_52_out, Shift[1], or_12_out);
  not not_27 (not_27_out, Shift[1]);
  and and_53 (and_53_out, not_27_out, or_11_out);
  and and_54 (and_54_out, Shift[1], or_13_out);
  not not_28 (not_28_out, Shift[1]);
  and and_55 (and_55_out, not_28_out, or_12_out);
  and and_56 (and_56_out, Shift[1], or_14_out);
  not not_29 (not_29_out, Shift[1]);
  and and_57 (and_57_out, not_29_out, or_13_out);
  and and_58 (and_58_out, Shift[1], or_15_out);
  not not_30 (not_30_out, Shift[1]);
  and and_59 (and_59_out, not_30_out, or_14_out);
  and and_60 (and_60_out, Shift[1], or_16_out);
  not not_31 (not_31_out, Shift[1]);
  and and_61 (and_61_out, not_31_out, or_15_out);
  and and_62 (and_62_out, Shift[1], Pad);
  not not_32 (not_32_out, Shift[1]);
  and and_63 (and_63_out, not_32_out, or_16_out);
  and and_64 (and_64_out, Shift[1], Pad);
  or or_17 (or_17_out, and_33_out, and_34_out);
  or or_18 (or_18_out, and_35_out, and_36_out);
  or or_19 (or_19_out, and_37_out, and_38_out);
  or or_20 (or_20_out, and_39_out, and_40_out);
  or or_21 (or_21_out, and_41_out, and_42_out);
  or or_22 (or_22_out, and_43_out, and_44_out);
  or or_23 (or_23_out, and_45_out, and_46_out);
  or or_24 (or_24_out, and_47_out, and_48_out);
  or or_25 (or_25_out, and_49_out, and_50_out);
  or or_26 (or_26_out, and_51_out, and_52_out);
  or or_27 (or_27_out, and_53_out, and_54_out);
  or or_28 (or_28_out, and_55_out, and_56_out);
  or or_29 (or_29_out, and_57_out, and_58_out);
  or or_30 (or_30_out, and_59_out, and_60_out);
  or or_31 (or_31_out, and_61_out, and_62_out);
  or or_32 (or_32_out, and_63_out, and_64_out);
  not not_33 (not_33_out, Shift[2]);
  not not_34 (not_34_out, Shift[2]);
  not not_35 (not_35_out, Shift[2]);
  not not_36 (not_36_out, Shift[2]);
  not not_37 (not_37_out, Shift[2]);
  not not_38 (not_38_out, Shift[2]);
  not not_39 (not_39_out, Shift[2]);
  not not_40 (not_40_out, Shift[2]);
  not not_41 (not_41_out, Shift[2]);
  not not_42 (not_42_out, Shift[2]);
  not not_43 (not_43_out, Shift[2]);
  not not_44 (not_44_out, Shift[2]);
  not not_45 (not_45_out, Shift[2]);
  not not_46 (not_46_out, Shift[2]);
  not not_47 (not_47_out, Shift[2]);
  not not_48 (not_48_out, Shift[2]);
  and and_65 (and_65_out, not_33_out, or_17_out);
  and and_66 (and_66_out, Shift[2], or_21_out);
  and and_67 (and_67_out, not_34_out, or_18_out);
  and and_68 (and_68_out, Shift[2], or_22_out);
  and and_69 (and_69_out, not_35_out, or_19_out);
  and and_70 (and_70_out, Shift[2], or_23_out);
  and and_71 (and_71_out, not_36_out, or_20_out);
  and and_72 (and_72_out, Shift[2], or_24_out);
  and and_73 (and_73_out, not_37_out, or_21_out);
  and and_74 (and_74_out, Shift[2], or_25_out);
  and and_75 (and_75_out, not_38_out, or_22_out);
  and and_76 (and_76_out, Shift[2], or_26_out);
  and and_77 (and_77_out, not_39_out, or_23_out);
  and and_78 (and_78_out, Shift[2], or_27_out);
  and and_79 (and_79_out, not_40_out, or_24_out);
  and and_80 (and_80_out, Shift[2], or_28_out);
  and and_81 (and_81_out, not_41_out, or_25_out);
  and and_82 (and_82_out, Shift[2], or_29_out);
  and and_83 (and_83_out, not_42_out, or_26_out);
  and and_84 (and_84_out, Shift[2], or_30_out);
  and and_85 (and_85_out, not_43_out, or_27_out);
  and and_86 (and_86_out, Shift[2], or_31_out);
  and and_87 (and_87_out, not_44_out, or_28_out);
  and and_88 (and_88_out, Shift[2], or_32_out);
  and and_89 (and_89_out, not_45_out, or_29_out);
  and and_90 (and_90_out, Shift[2], Pad);
  and and_91 (and_91_out, not_46_out, or_30_out);
  and and_92 (and_92_out, Shift[2], Pad);
  and and_93 (and_93_out, not_47_out, or_31_out);
  and and_94 (and_94_out, Shift[2], Pad);
  and and_95 (and_95_out, not_48_out, or_32_out);
  and and_96 (and_96_out, Shift[2], Pad);
  or or_33 (or_33_out, and_65_out, and_66_out);
  or or_34 (or_34_out, and_67_out, and_68_out);
  or or_35 (or_35_out, and_69_out, and_70_out);
  or or_36 (or_36_out, and_71_out, and_72_out);
  or or_37 (or_37_out, and_73_out, and_74_out);
  or or_38 (or_38_out, and_75_out, and_76_out);
  or or_39 (or_39_out, and_77_out, and_78_out);
  or or_40 (or_40_out, and_79_out, and_80_out);
  or or_41 (or_41_out, and_81_out, and_82_out);
  or or_42 (or_42_out, and_83_out, and_84_out);
  or or_43 (or_43_out, and_85_out, and_86_out);
  or or_44 (or_44_out, and_87_out, and_88_out);
  or or_45 (or_45_out, and_89_out, and_90_out);
  or or_46 (or_46_out, and_91_out, and_92_out);
  or or_47 (or_47_out, and_93_out, and_94_out);
  or or_48 (or_48_out, and_95_out, and_96_out);
  not not_49 (not_49_out, Shift[3]);
  not not_50 (not_50_out, Shift[3]);
  not not_51 (not_51_out, Shift[3]);
  not not_52 (not_52_out, Shift[3]);
  not not_53 (not_53_out, Shift[3]);
  not not_54 (not_54_out, Shift[3]);
  not not_55 (not_55_out, Shift[3]);
  not not_56 (not_56_out, Shift[3]);
  not not_57 (not_57_out, Shift[3]);
  not not_58 (not_58_out, Shift[3]);
  not not_59 (not_59_out, Shift[3]);
  not not_60 (not_60_out, Shift[3]);
  not not_61 (not_61_out, Shift[3]);
  not not_62 (not_62_out, Shift[3]);
  not not_63 (not_63_out, Shift[3]);
  not not_64 (not_64_out, Shift[3]);
  and and_97 (and_97_out, not_49_out, or_33_out);
  and and_98 (and_98_out, Shift[3], or_41_out);
  and and_99 (and_99_out, not_50_out, or_34_out);
  and and_100 (and_100_out, Shift[3], or_42_out);
  and and_101 (and_101_out, not_51_out, or_35_out);
  and and_102 (and_102_out, Shift[3], or_43_out);
  and and_103 (and_103_out, not_52_out, or_36_out);
  and and_104 (and_104_out, Shift[3], or_44_out);
  and and_105 (and_105_out, not_53_out, or_37_out);
  and and_106 (and_106_out, Shift[3], or_45_out);
  and and_107 (and_107_out, not_54_out, or_38_out);
  and and_108 (and_108_out, Shift[3], or_46_out);
  and and_109 (and_109_out, not_55_out, or_39_out);
  and and_110 (and_110_out, Shift[3], or_47_out);
  and and_111 (and_111_out, not_56_out, or_40_out);
  and and_112 (and_112_out, Shift[3], or_48_out);
  and and_113 (and_113_out, not_57_out, or_41_out);
  and and_114 (and_114_out, Shift[3], Pad);
  and and_115 (and_115_out, not_58_out, or_42_out);
  and and_116 (and_116_out, Shift[3], Pad);
  and and_117 (and_117_out, not_59_out, or_43_out);
  and and_118 (and_118_out, Shift[3], Pad);
  and and_119 (and_119_out, not_60_out, or_44_out);
  and and_120 (and_120_out, Shift[3], Pad);
  and and_121 (and_121_out, not_61_out, or_45_out);
  and and_122 (and_122_out, Shift[3], Pad);
  and and_123 (and_123_out, not_62_out, or_46_out);
  and and_124 (and_124_out, Shift[3], Pad);
  and and_125 (and_125_out, not_63_out, or_47_out);
  and and_126 (and_126_out, Shift[3], Pad);
  and and_127 (and_127_out, not_64_out, or_48_out);
  and and_128 (and_128_out, Shift[3], Pad);
  or or_49 (Resutl[0], and_97_out, and_98_out);
  or or_50 (Resutl[1], and_99_out, and_100_out);
  or or_51 (Resutl[2], and_101_out, and_102_out);
  or or_52 (Resutl[3], and_103_out, and_104_out);
  or or_53 (Resutl[4], and_105_out, and_106_out);
  or or_54 (Resutl[5], and_107_out, and_108_out);
  or or_55 (Resutl[6], and_109_out, and_110_out);
  or or_56 (Resutl[7], and_111_out, and_112_out);
  or or_57 (Resutl[8], and_113_out, and_114_out);
  or or_58 (Resutl[9], and_115_out, and_116_out);
  or or_59 (Resutl[10], and_117_out, and_118_out);
  or or_60 (Resutl[11], and_119_out, and_120_out);
  or or_61 (Resutl[12], and_121_out, and_122_out);
  or or_62 (Resutl[13], and_123_out, and_124_out);
  or or_63 (Resutl[14], and_125_out, and_126_out);
  or or_64 (Resutl[15], and_127_out, and_128_out);
endmodule

module SHL (
  input  [15:0] X,
  input  [4:0] Shift,
  input  Pad,
  output [15:0] Resutl
);

  wire and_1_out, and_2_out, and_3_out, and_4_out, and_5_out, and_6_out, and_7_out, and_8_out, and_9_out,
       and_10_out, and_11_out, and_12_out, and_13_out, and_14_out, and_15_out, and_16_out, and_17_out,
       and_18_out, and_19_out, and_20_out, and_21_out, and_22_out, and_23_out, and_24_out, and_25_out,
       and_26_out, and_27_out, and_28_out, and_29_out, and_30_out, and_31_out, and_32_out, and_33_out,
       and_34_out, and_35_out, and_36_out, and_37_out, and_38_out, and_39_out, and_40_out, and_41_out,
       and_42_out, and_43_out, and_44_out, and_45_out, and_46_out, and_47_out, and_48_out, and_49_out,
       and_50_out, and_51_out, and_52_out, and_53_out, and_54_out, and_55_out, and_56_out, and_57_out,
       and_58_out, and_59_out, and_60_out, and_61_out, and_62_out, and_63_out, and_64_out, and_65_out,
       and_66_out, and_67_out, and_68_out, and_69_out, and_70_out, and_71_out, and_72_out, and_73_out,
       and_74_out, and_75_out, and_76_out, and_77_out, and_78_out, and_79_out, and_80_out, and_81_out,
       and_82_out, and_83_out, and_84_out, and_85_out, and_86_out, and_87_out, and_88_out, and_89_out,
       and_90_out, and_91_out, and_92_out, and_93_out, and_94_out, and_95_out, and_96_out, and_97_out,
       and_98_out, and_99_out, and_100_out, and_101_out, and_102_out, and_103_out, and_104_out, and_105_out,
       and_106_out, and_107_out, and_108_out, and_109_out, and_110_out, and_111_out, and_112_out,
       and_113_out, and_114_out, and_115_out, and_116_out, and_117_out, and_118_out, and_119_out,
       and_120_out, and_121_out, and_122_out, and_123_out, and_124_out, and_125_out, and_126_out,
       and_127_out, and_128_out, not_1_out, not_2_out, not_3_out, not_4_out, not_5_out, not_6_out, not_7_out,
       not_8_out, not_9_out, not_10_out, not_11_out, not_12_out, not_13_out, not_14_out, not_15_out,
       not_16_out, not_17_out, not_18_out, not_19_out, not_20_out, not_21_out, not_22_out, not_23_out,
       not_24_out, not_25_out, not_26_out, not_27_out, not_28_out, not_29_out, not_30_out, not_31_out,
       not_32_out, not_33_out, not_34_out, not_35_out, not_36_out, not_37_out, not_38_out, not_39_out,
       not_40_out, not_41_out, not_42_out, not_43_out, not_44_out, not_45_out, not_46_out, not_47_out,
       not_48_out, not_49_out, not_50_out, not_51_out, not_52_out, not_53_out, not_54_out, not_55_out,
       not_56_out, not_57_out, not_58_out, not_59_out, not_60_out, not_61_out, not_62_out, not_63_out,
       not_64_out, or_1_out, or_2_out, or_3_out, or_4_out, or_5_out, or_6_out, or_7_out, or_8_out, or_9_out,
       or_10_out, or_11_out, or_12_out, or_13_out, or_14_out, or_15_out, or_16_out, or_17_out, or_18_out,
       or_19_out, or_20_out, or_21_out, or_22_out, or_23_out, or_24_out, or_25_out, or_26_out, or_27_out,
       or_28_out, or_29_out, or_30_out, or_31_out, or_32_out, or_33_out, or_34_out, or_35_out, or_36_out,
       or_37_out, or_38_out, or_39_out, or_40_out, or_41_out, or_42_out, or_43_out, or_44_out, or_45_out,
       or_46_out, or_47_out, or_48_out;

  not not_1 (not_1_out, Shift[0]);
  and and_1 (and_1_out, not_1_out, X[15]);
  and and_2 (and_2_out, Shift[0], X[14]);
  not not_2 (not_2_out, Shift[0]);
  and and_3 (and_3_out, not_2_out, X[14]);
  and and_4 (and_4_out, Shift[0], X[13]);
  not not_3 (not_3_out, Shift[0]);
  and and_5 (and_5_out, not_3_out, X[13]);
  and and_6 (and_6_out, Shift[0], X[12]);
  not not_4 (not_4_out, Shift[0]);
  and and_7 (and_7_out, not_4_out, X[12]);
  and and_8 (and_8_out, Shift[0], X[11]);
  not not_5 (not_5_out, Shift[0]);
  and and_9 (and_9_out, not_5_out, X[11]);
  and and_10 (and_10_out, Shift[0], X[10]);
  not not_6 (not_6_out, Shift[0]);
  and and_11 (and_11_out, not_6_out, X[10]);
  and and_12 (and_12_out, Shift[0], X[9]);
  not not_7 (not_7_out, Shift[0]);
  and and_13 (and_13_out, not_7_out, X[9]);
  and and_14 (and_14_out, Shift[0], X[8]);
  not not_8 (not_8_out, Shift[0]);
  and and_15 (and_15_out, not_8_out, X[8]);
  and and_16 (and_16_out, Shift[0], X[7]);
  not not_9 (not_9_out, Shift[0]);
  and and_17 (and_17_out, not_9_out, X[7]);
  and and_18 (and_18_out, Shift[0], X[6]);
  not not_10 (not_10_out, Shift[0]);
  and and_19 (and_19_out, not_10_out, X[6]);
  and and_20 (and_20_out, Shift[0], X[5]);
  not not_11 (not_11_out, Shift[0]);
  and and_21 (and_21_out, not_11_out, X[5]);
  and and_22 (and_22_out, Shift[0], X[4]);
  not not_12 (not_12_out, Shift[0]);
  and and_23 (and_23_out, not_12_out, X[4]);
  and and_24 (and_24_out, Shift[0], X[3]);
  not not_13 (not_13_out, Shift[0]);
  and and_25 (and_25_out, not_13_out, X[3]);
  and and_26 (and_26_out, Shift[0], X[2]);
  not not_14 (not_14_out, Shift[0]);
  and and_27 (and_27_out, not_14_out, X[2]);
  and and_28 (and_28_out, Shift[0], X[1]);
  not not_15 (not_15_out, Shift[0]);
  and and_29 (and_29_out, not_15_out, X[1]);
  and and_30 (and_30_out, Shift[0], X[0]);
  not not_16 (not_16_out, Shift[0]);
  and and_31 (and_31_out, not_16_out, X[0]);
  and and_32 (and_32_out, Shift[0], Pad);
  or or_1 (or_1_out, and_1_out, and_2_out);
  or or_2 (or_2_out, and_3_out, and_4_out);
  or or_3 (or_3_out, and_5_out, and_6_out);
  or or_4 (or_4_out, and_7_out, and_8_out);
  or or_5 (or_5_out, and_9_out, and_10_out);
  or or_6 (or_6_out, and_11_out, and_12_out);
  or or_7 (or_7_out, and_13_out, and_14_out);
  or or_8 (or_8_out, and_15_out, and_16_out);
  or or_9 (or_9_out, and_17_out, and_18_out);
  or or_10 (or_10_out, and_19_out, and_20_out);
  or or_11 (or_11_out, and_21_out, and_22_out);
  or or_12 (or_12_out, and_23_out, and_24_out);
  or or_13 (or_13_out, and_25_out, and_26_out);
  or or_14 (or_14_out, and_27_out, and_28_out);
  or or_15 (or_15_out, and_29_out, and_30_out);
  or or_16 (or_16_out, and_31_out, and_32_out);
  not not_17 (not_17_out, Shift[1]);
  not not_18 (not_18_out, Shift[1]);
  not not_19 (not_19_out, Shift[1]);
  not not_20 (not_20_out, Shift[1]);
  not not_21 (not_21_out, Shift[1]);
  not not_22 (not_22_out, Shift[1]);
  not not_23 (not_23_out, Shift[1]);
  not not_24 (not_24_out, Shift[1]);
  not not_25 (not_25_out, Shift[1]);
  not not_26 (not_26_out, Shift[1]);
  not not_27 (not_27_out, Shift[1]);
  not not_28 (not_28_out, Shift[1]);
  not not_29 (not_29_out, Shift[1]);
  not not_30 (not_30_out, Shift[1]);
  not not_31 (not_31_out, Shift[1]);
  not not_32 (not_32_out, Shift[1]);
  and and_33 (and_33_out, not_17_out, or_1_out);
  and and_34 (and_34_out, Shift[1], or_3_out);
  and and_35 (and_35_out, not_18_out, or_2_out);
  and and_36 (and_36_out, Shift[1], or_4_out);
  and and_37 (and_37_out, not_19_out, or_3_out);
  and and_38 (and_38_out, Shift[1], or_5_out);
  and and_39 (and_39_out, not_20_out, or_4_out);
  and and_40 (and_40_out, Shift[1], or_6_out);
  and and_41 (and_41_out, not_21_out, or_5_out);
  and and_42 (and_42_out, Shift[1], or_7_out);
  and and_43 (and_43_out, not_22_out, or_6_out);
  and and_44 (and_44_out, Shift[1], or_8_out);
  and and_45 (and_45_out, not_23_out, or_7_out);
  and and_46 (and_46_out, Shift[1], or_9_out);
  and and_47 (and_47_out, not_24_out, or_8_out);
  and and_48 (and_48_out, Shift[1], or_10_out);
  and and_49 (and_49_out, not_25_out, or_9_out);
  and and_50 (and_50_out, Shift[1], or_11_out);
  and and_51 (and_51_out, not_26_out, or_10_out);
  and and_52 (and_52_out, Shift[1], or_12_out);
  and and_53 (and_53_out, not_27_out, or_11_out);
  and and_54 (and_54_out, Shift[1], or_13_out);
  and and_55 (and_55_out, not_28_out, or_12_out);
  and and_56 (and_56_out, Shift[1], or_14_out);
  and and_57 (and_57_out, not_29_out, or_13_out);
  and and_58 (and_58_out, Shift[1], or_15_out);
  and and_59 (and_59_out, not_30_out, or_14_out);
  and and_60 (and_60_out, Shift[1], or_16_out);
  and and_61 (and_61_out, not_31_out, or_15_out);
  and and_62 (and_62_out, Shift[1], Pad);
  and and_63 (and_63_out, not_32_out, or_16_out);
  and and_64 (and_64_out, Shift[1], Pad);
  or or_17 (or_17_out, and_33_out, and_34_out);
  or or_18 (or_18_out, and_35_out, and_36_out);
  or or_19 (or_19_out, and_37_out, and_38_out);
  or or_20 (or_20_out, and_39_out, and_40_out);
  or or_21 (or_21_out, and_41_out, and_42_out);
  or or_22 (or_22_out, and_43_out, and_44_out);
  or or_23 (or_23_out, and_45_out, and_46_out);
  or or_24 (or_24_out, and_47_out, and_48_out);
  or or_25 (or_25_out, and_49_out, and_50_out);
  or or_26 (or_26_out, and_51_out, and_52_out);
  or or_27 (or_27_out, and_53_out, and_54_out);
  or or_28 (or_28_out, and_55_out, and_56_out);
  or or_29 (or_29_out, and_57_out, and_58_out);
  or or_30 (or_30_out, and_59_out, and_60_out);
  or or_31 (or_31_out, and_61_out, and_62_out);
  or or_32 (or_32_out, and_63_out, and_64_out);
  not not_33 (not_33_out, Shift[2]);
  and and_65 (and_65_out, not_33_out, or_17_out);
  and and_66 (and_66_out, Shift[2], or_21_out);
  not not_34 (not_34_out, Shift[2]);
  and and_67 (and_67_out, not_34_out, or_18_out);
  and and_68 (and_68_out, Shift[2], or_22_out);
  not not_35 (not_35_out, Shift[2]);
  and and_69 (and_69_out, not_35_out, or_19_out);
  and and_70 (and_70_out, Shift[2], or_23_out);
  not not_36 (not_36_out, Shift[2]);
  and and_71 (and_71_out, not_36_out, or_20_out);
  and and_72 (and_72_out, Shift[2], or_24_out);
  not not_37 (not_37_out, Shift[2]);
  and and_73 (and_73_out, not_37_out, or_21_out);
  and and_74 (and_74_out, Shift[2], or_25_out);
  not not_38 (not_38_out, Shift[2]);
  and and_75 (and_75_out, not_38_out, or_22_out);
  and and_76 (and_76_out, Shift[2], or_26_out);
  not not_39 (not_39_out, Shift[2]);
  and and_77 (and_77_out, not_39_out, or_23_out);
  and and_78 (and_78_out, Shift[2], or_27_out);
  not not_40 (not_40_out, Shift[2]);
  and and_79 (and_79_out, not_40_out, or_24_out);
  and and_80 (and_80_out, Shift[2], or_28_out);
  not not_41 (not_41_out, Shift[2]);
  and and_81 (and_81_out, not_41_out, or_25_out);
  and and_82 (and_82_out, Shift[2], or_29_out);
  not not_42 (not_42_out, Shift[2]);
  and and_83 (and_83_out, not_42_out, or_26_out);
  and and_84 (and_84_out, Shift[2], or_30_out);
  not not_43 (not_43_out, Shift[2]);
  and and_85 (and_85_out, not_43_out, or_27_out);
  and and_86 (and_86_out, Shift[2], or_31_out);
  not not_44 (not_44_out, Shift[2]);
  and and_87 (and_87_out, not_44_out, or_28_out);
  and and_88 (and_88_out, Shift[2], or_32_out);
  not not_45 (not_45_out, Shift[2]);
  and and_89 (and_89_out, not_45_out, or_29_out);
  and and_90 (and_90_out, Shift[2], Pad);
  not not_46 (not_46_out, Shift[2]);
  and and_91 (and_91_out, not_46_out, or_30_out);
  and and_92 (and_92_out, Shift[2], Pad);
  not not_47 (not_47_out, Shift[2]);
  and and_93 (and_93_out, not_47_out, or_31_out);
  and and_94 (and_94_out, Shift[2], Pad);
  not not_48 (not_48_out, Shift[2]);
  and and_95 (and_95_out, not_48_out, or_32_out);
  and and_96 (and_96_out, Shift[2], Pad);
  or or_33 (or_33_out, and_65_out, and_66_out);
  or or_34 (or_34_out, and_67_out, and_68_out);
  or or_35 (or_35_out, and_69_out, and_70_out);
  or or_36 (or_36_out, and_71_out, and_72_out);
  or or_37 (or_37_out, and_73_out, and_74_out);
  or or_38 (or_38_out, and_75_out, and_76_out);
  or or_39 (or_39_out, and_77_out, and_78_out);
  or or_40 (or_40_out, and_79_out, and_80_out);
  or or_41 (or_41_out, and_81_out, and_82_out);
  or or_42 (or_42_out, and_83_out, and_84_out);
  or or_43 (or_43_out, and_85_out, and_86_out);
  or or_44 (or_44_out, and_87_out, and_88_out);
  or or_45 (or_45_out, and_89_out, and_90_out);
  or or_46 (or_46_out, and_91_out, and_92_out);
  or or_47 (or_47_out, and_93_out, and_94_out);
  or or_48 (or_48_out, and_95_out, and_96_out);
  not not_49 (not_49_out, Shift[3]);
  and and_97 (and_97_out, not_49_out, or_33_out);
  and and_98 (and_98_out, Shift[3], or_41_out);
  not not_50 (not_50_out, Shift[3]);
  and and_99 (and_99_out, not_50_out, or_34_out);
  and and_100 (and_100_out, Shift[3], or_42_out);
  not not_51 (not_51_out, Shift[3]);
  and and_101 (and_101_out, not_51_out, or_35_out);
  and and_102 (and_102_out, Shift[3], or_43_out);
  not not_52 (not_52_out, Shift[3]);
  and and_103 (and_103_out, not_52_out, or_36_out);
  and and_104 (and_104_out, Shift[3], or_44_out);
  not not_53 (not_53_out, Shift[3]);
  and and_105 (and_105_out, not_53_out, or_37_out);
  and and_106 (and_106_out, Shift[3], or_45_out);
  not not_54 (not_54_out, Shift[3]);
  and and_107 (and_107_out, not_54_out, or_38_out);
  and and_108 (and_108_out, Shift[3], or_46_out);
  not not_55 (not_55_out, Shift[3]);
  and and_109 (and_109_out, not_55_out, or_39_out);
  and and_110 (and_110_out, Shift[3], or_47_out);
  not not_56 (not_56_out, Shift[3]);
  and and_111 (and_111_out, not_56_out, or_40_out);
  and and_112 (and_112_out, Shift[3], or_48_out);
  not not_57 (not_57_out, Shift[3]);
  and and_113 (and_113_out, not_57_out, or_41_out);
  and and_114 (and_114_out, Shift[3], Pad);
  not not_58 (not_58_out, Shift[3]);
  and and_115 (and_115_out, not_58_out, or_42_out);
  and and_116 (and_116_out, Shift[3], Pad);
  not not_59 (not_59_out, Shift[3]);
  and and_117 (and_117_out, not_59_out, or_43_out);
  and and_118 (and_118_out, Shift[3], Pad);
  not not_60 (not_60_out, Shift[3]);
  and and_119 (and_119_out, not_60_out, or_44_out);
  and and_120 (and_120_out, Shift[3], Pad);
  not not_61 (not_61_out, Shift[3]);
  and and_121 (and_121_out, not_61_out, or_45_out);
  and and_122 (and_122_out, Shift[3], Pad);
  not not_62 (not_62_out, Shift[3]);
  and and_123 (and_123_out, not_62_out, or_46_out);
  and and_124 (and_124_out, Shift[3], Pad);
  not not_63 (not_63_out, Shift[3]);
  and and_125 (and_125_out, not_63_out, or_47_out);
  and and_126 (and_126_out, Shift[3], Pad);
  not not_64 (not_64_out, Shift[3]);
  and and_127 (and_127_out, not_64_out, or_48_out);
  and and_128 (and_128_out, Shift[3], Pad);
  or or_49 (Resutl[15], and_97_out, and_98_out);
  or or_50 (Resutl[14], and_99_out, and_100_out);
  or or_51 (Resutl[13], and_101_out, and_102_out);
  or or_52 (Resutl[12], and_103_out, and_104_out);
  or or_53 (Resutl[11], and_105_out, and_106_out);
  or or_54 (Resutl[10], and_107_out, and_108_out);
  or or_55 (Resutl[9], and_109_out, and_110_out);
  or or_56 (Resutl[8], and_111_out, and_112_out);
  or or_57 (Resutl[7], and_113_out, and_114_out);
  or or_58 (Resutl[6], and_115_out, and_116_out);
  or or_59 (Resutl[5], and_117_out, and_118_out);
  or or_60 (Resutl[4], and_119_out, and_120_out);
  or or_61 (Resutl[3], and_121_out, and_122_out);
  or or_62 (Resutl[2], and_123_out, and_124_out);
  or or_63 (Resutl[1], and_125_out, and_126_out);
  or or_64 (Resutl[0], and_127_out, and_128_out);
endmodule

module GPRs (
  input  RegWrite_enable,
  input  [2:0] regW,
  input  [15:0] Data_In,
  input  Clock,
  input  [2:0] reg0_idx,
  input  [2:0] reg1_idx,
  output [15:0] reg0,
  output [15:0] reg1
);

  wire and_1_out, and_2_out, and_3_out, and_4_out, and_5_out, and_6_out, and_7_out, and_8_out, and_9_out,
       and_10_out, and_11_out, and_12_out, and_13_out, and_14_out, and_15_out, and_16_out, not_1_out,
       not_2_out, not_3_out, not_4_out, not_5_out, not_6_out, not_7_out, not_8_out, not_9_out, not_10_out,
       not_11_out, not_12_out;
  wire [15:0] rx0_data_out, rx1_data_out, rx2_data_out, rx3_data_out, rx4_data_out, rx5_data_out,
       rx6_data_out, rx7_data_out;

  not not_1 (not_1_out, regW[0]);
  not not_2 (not_2_out, regW[1]);
  not not_3 (not_3_out, regW[2]);
  not not_4 (not_4_out, regW[1]);
  not not_5 (not_5_out, regW[2]);
  not not_6 (not_6_out, regW[0]);
  not not_7 (not_7_out, regW[2]);
  not not_8 (not_8_out, regW[2]);
  not not_9 (not_9_out, regW[0]);
  not not_10 (not_10_out, regW[1]);
  not not_11 (not_11_out, regW[1]);
  not not_12 (not_12_out, regW[0]);
  and and_1 (and_1_out, not_1_out, not_2_out, not_3_out);
  and and_2 (and_2_out, regW[0], not_4_out, not_5_out);
  and and_3 (and_3_out, not_6_out, regW[1], not_7_out);
  and and_4 (and_4_out, regW[0], regW[1], not_8_out);
  and and_5 (and_5_out, not_9_out, not_10_out, regW[2]);
  and and_6 (and_6_out, regW[0], not_11_out, regW[2]);
  and and_7 (and_7_out, not_12_out, regW[1], regW[2]);
  and and_8 (and_8_out, regW[0], regW[1], regW[2]);
  and and_9 (and_9_out, RegWrite_enable, and_1_out);
  and and_10 (and_10_out, RegWrite_enable, and_2_out);
  and and_11 (and_11_out, RegWrite_enable, and_3_out);
  and and_12 (and_12_out, RegWrite_enable, and_4_out);
  and and_13 (and_13_out, RegWrite_enable, and_5_out);
  and and_14 (and_14_out, RegWrite_enable, and_6_out);
  and and_15 (and_15_out, RegWrite_enable, and_7_out);
  and and_16 (and_16_out, RegWrite_enable, and_8_out);
  Reg16Bit rx0 (.Data_in(Data_In), .write_enable(and_9_out), .Clock(Clock), .Data_out(rx0_data_out));
  Reg16Bit rx1 (.Data_in(Data_In), .write_enable(and_10_out), .Clock(Clock), .Data_out(rx1_data_out));
  Reg16Bit rx2 (.Data_in(Data_In), .write_enable(and_11_out), .Clock(Clock), .Data_out(rx2_data_out));
  Reg16Bit rx3 (.Data_in(Data_In), .write_enable(and_12_out), .Clock(Clock), .Data_out(rx3_data_out));
  Reg16Bit rx4 (.Data_in(Data_In), .write_enable(and_13_out), .Clock(Clock), .Data_out(rx4_data_out));
  Reg16Bit rx5 (.Data_in(Data_In), .write_enable(and_14_out), .Clock(Clock), .Data_out(rx5_data_out));
  Reg16Bit rx6 (.Data_in(Data_In), .write_enable(and_15_out), .Clock(Clock), .Data_out(rx6_data_out));
  Reg16Bit rx7 (.Data_in(Data_In), .write_enable(and_16_out), .Clock(Clock), .Data_out(rx7_data_out));
  MUX8_1 mux8_1_1 (
    .rx_sel(reg0_idx), .rx0(rx0_data_out), .rx1(rx1_data_out), .rx2(rx2_data_out), .rx3(rx3_data_out),
    .rx4(rx4_data_out), .rx5(rx5_data_out), .rx6(rx6_data_out), .rx7(rx7_data_out), .Reading(reg0));
  MUX8_1 mux8_1_2 (
    .rx_sel(reg1_idx), .rx0(rx0_data_out), .rx1(rx1_data_out), .rx2(rx2_data_out), .rx3(rx3_data_out),
    .rx4(rx4_data_out), .rx5(rx5_data_out), .rx6(rx6_data_out), .rx7(rx7_data_out), .Reading(reg1));
endmodule

module Reg16Bit (
  input  [15:0] Data_in,
  input  write_enable,
  input  Clock,
  output [15:0] Data_out
);

  wire and_1_out, and_2_out, and_3_out, and_4_out, and_5_out, and_6_out, and_7_out, and_8_out, and_9_out,
       and_10_out, and_11_out, and_12_out, and_13_out, and_14_out, and_15_out, and_16_out, and_17_out,
       and_18_out, and_19_out, and_20_out, and_21_out, and_22_out, and_23_out, and_24_out, and_25_out,
       and_26_out, and_27_out, and_28_out, and_29_out, and_30_out, and_31_out, and_32_out, and_33_out,
       and_34_out, and_35_out, and_36_out, and_37_out, and_38_out, and_39_out, and_40_out, and_41_out,
       and_42_out, and_43_out, and_44_out, and_45_out, and_46_out, and_47_out, and_48_out, and_49_out,
       and_50_out, and_51_out, and_52_out, and_53_out, and_54_out, and_55_out, and_56_out, and_57_out,
       and_58_out, and_59_out, and_60_out, and_61_out, and_62_out, and_63_out, and_64_out, and_65_out,
       and_66_out, and_67_out, and_68_out, and_69_out, and_70_out, and_71_out, and_72_out, and_73_out,
       and_74_out, and_75_out, and_76_out, and_77_out, and_78_out, and_79_out, and_80_out, and_81_out,
       and_82_out, and_83_out, and_84_out, and_85_out, and_86_out, and_87_out, and_88_out, and_89_out,
       and_90_out, and_91_out, and_92_out, and_93_out, and_94_out, and_95_out, and_96_out, nor_1_out,
       nor_2_out, nor_3_out, nor_4_out, nor_5_out, nor_6_out, nor_7_out, nor_8_out, nor_9_out, nor_10_out,
       nor_11_out, nor_12_out, nor_13_out, nor_14_out, nor_15_out, nor_16_out, nor_17_out, nor_18_out,
       nor_19_out, nor_20_out, nor_21_out, nor_22_out, nor_23_out, nor_24_out, nor_25_out, nor_26_out,
       nor_27_out, nor_28_out, nor_29_out, nor_30_out, nor_31_out, nor_32_out, nor_34_out, nor_36_out,
       nor_38_out, nor_40_out, nor_42_out, nor_44_out, nor_46_out, nor_48_out, nor_50_out, nor_52_out,
       nor_54_out, nor_56_out, nor_58_out, nor_60_out, nor_62_out, nor_64_out, not_1_out, not_2_out,
       not_3_out, not_4_out, not_5_out, not_6_out, not_7_out, not_8_out, not_9_out, not_10_out, not_11_out,
       not_12_out, not_13_out, not_14_out, not_15_out, not_16_out, not_17_out, not_18_out, not_19_out,
       not_20_out, not_21_out, not_22_out, not_23_out, not_24_out, not_25_out, not_26_out, not_27_out,
       not_28_out, not_29_out, not_30_out, not_31_out, not_32_out, not_33_out, not_34_out, not_35_out,
       not_36_out, not_37_out, not_38_out, not_39_out, not_40_out, not_41_out, not_42_out, not_43_out,
       not_44_out, not_45_out, not_46_out, not_47_out, not_48_out, not_49_out, not_50_out, or_1_out,
       or_2_out, or_3_out, or_4_out, or_5_out, or_6_out, or_7_out, or_8_out, or_9_out, or_10_out, or_11_out,
       or_12_out, or_13_out, or_14_out, or_15_out, or_16_out;

  not not_1 (not_1_out, write_enable);
  and and_1 (and_1_out, Data_out[0], not_1_out);
  and and_2 (and_2_out, Data_in[0], not_2_out);
  not not_2 (not_2_out, not_1_out);
  and and_3 (and_3_out, Data_out[1], not_1_out);
  and and_4 (and_4_out, Data_in[1], not_3_out);
  not not_3 (not_3_out, not_1_out);
  and and_5 (and_5_out, Data_out[2], not_1_out);
  and and_6 (and_6_out, Data_in[2], not_4_out);
  not not_4 (not_4_out, not_1_out);
  and and_7 (and_7_out, Data_out[3], not_1_out);
  and and_8 (and_8_out, Data_in[3], not_5_out);
  not not_5 (not_5_out, not_1_out);
  and and_9 (and_9_out, Data_out[4], not_1_out);
  and and_10 (and_10_out, Data_in[4], not_6_out);
  not not_6 (not_6_out, not_1_out);
  and and_11 (and_11_out, Data_out[5], not_1_out);
  and and_12 (and_12_out, Data_in[5], not_7_out);
  not not_7 (not_7_out, not_1_out);
  and and_13 (and_13_out, Data_out[6], not_1_out);
  and and_14 (and_14_out, Data_in[6], not_8_out);
  not not_8 (not_8_out, not_1_out);
  and and_15 (and_15_out, Data_out[7], not_1_out);
  and and_16 (and_16_out, Data_in[7], not_9_out);
  not not_9 (not_9_out, not_1_out);
  and and_17 (and_17_out, Data_out[8], not_1_out);
  and and_18 (and_18_out, Data_in[8], not_10_out);
  not not_10 (not_10_out, not_1_out);
  and and_19 (and_19_out, Data_out[9], not_1_out);
  and and_20 (and_20_out, Data_in[9], not_11_out);
  not not_11 (not_11_out, not_1_out);
  and and_21 (and_21_out, Data_out[10], not_1_out);
  and and_22 (and_22_out, Data_in[10], not_12_out);
  not not_12 (not_12_out, not_1_out);
  and and_23 (and_23_out, Data_out[11], not_1_out);
  and and_24 (and_24_out, Data_in[11], not_13_out);
  not not_13 (not_13_out, not_1_out);
  and and_25 (and_25_out, Data_out[12], not_1_out);
  and and_26 (and_26_out, Data_in[12], not_14_out);
  not not_14 (not_14_out, not_1_out);
  and and_27 (and_27_out, Data_out[13], not_1_out);
  and and_28 (and_28_out, Data_in[13], not_15_out);
  not not_15 (not_15_out, not_1_out);
  and and_29 (and_29_out, Data_out[14], not_1_out);
  and and_30 (and_30_out, Data_in[14], not_16_out);
  not not_16 (not_16_out, not_1_out);
  and and_31 (and_31_out, Data_out[15], not_1_out);
  and and_32 (and_32_out, Data_in[15], not_17_out);
  not not_17 (not_17_out, not_1_out);
  or or_1 (or_1_out, and_1_out, and_2_out);
  or or_2 (or_2_out, and_3_out, and_4_out);
  or or_3 (or_3_out, and_5_out, and_6_out);
  or or_4 (or_4_out, and_7_out, and_8_out);
  or or_5 (or_5_out, and_9_out, and_10_out);
  or or_6 (or_6_out, and_11_out, and_12_out);
  or or_7 (or_7_out, and_13_out, and_14_out);
  or or_8 (or_8_out, and_15_out, and_16_out);
  or or_9 (or_9_out, and_17_out, and_18_out);
  or or_10 (or_10_out, and_19_out, and_20_out);
  or or_11 (or_11_out, and_21_out, and_22_out);
  or or_12 (or_12_out, and_23_out, and_24_out);
  or or_13 (or_13_out, and_25_out, and_26_out);
  or or_14 (or_14_out, and_27_out, and_28_out);
  or or_15 (or_15_out, and_29_out, and_30_out);
  or or_16 (or_16_out, and_31_out, and_32_out);
  not not_18 (not_18_out, or_1_out);
  not not_19 (not_19_out, or_2_out);
  not not_20 (not_20_out, or_3_out);
  not not_21 (not_21_out, or_4_out);
  not not_22 (not_22_out, or_5_out);
  not not_23 (not_23_out, or_6_out);
  not not_24 (not_24_out, or_7_out);
  not not_25 (not_25_out, or_8_out);
  not not_26 (not_26_out, or_9_out);
  not not_27 (not_27_out, or_10_out);
  not not_28 (not_28_out, or_11_out);
  not not_29 (not_29_out, or_12_out);
  not not_30 (not_30_out, or_13_out);
  not not_31 (not_31_out, or_14_out);
  not not_32 (not_32_out, or_15_out);
  not not_33 (not_33_out, or_16_out);
  not not_34 (not_34_out, Clock);
  and and_33 (and_33_out, not_18_out, Clock);
  and and_34 (and_34_out, Clock, or_1_out);
  and and_35 (and_35_out, not_19_out, Clock);
  and and_36 (and_36_out, Clock, or_2_out);
  and and_37 (and_37_out, not_20_out, Clock);
  and and_38 (and_38_out, Clock, or_3_out);
  and and_39 (and_39_out, not_21_out, Clock);
  and and_40 (and_40_out, Clock, or_4_out);
  and and_41 (and_41_out, not_22_out, Clock);
  and and_42 (and_42_out, Clock, or_5_out);
  and and_43 (and_43_out, not_23_out, Clock);
  and and_44 (and_44_out, Clock, or_6_out);
  and and_45 (and_45_out, not_24_out, Clock);
  and and_46 (and_46_out, Clock, or_7_out);
  and and_47 (and_47_out, not_25_out, Clock);
  and and_48 (and_48_out, Clock, or_8_out);
  and and_49 (and_49_out, not_26_out, Clock);
  and and_50 (and_50_out, Clock, or_9_out);
  and and_51 (and_51_out, not_27_out, Clock);
  and and_52 (and_52_out, Clock, or_10_out);
  and and_53 (and_53_out, not_28_out, Clock);
  and and_54 (and_54_out, Clock, or_11_out);
  and and_55 (and_55_out, not_29_out, Clock);
  and and_56 (and_56_out, Clock, or_12_out);
  and and_57 (and_57_out, not_30_out, Clock);
  and and_58 (and_58_out, Clock, or_13_out);
  and and_59 (and_59_out, not_31_out, Clock);
  and and_60 (and_60_out, Clock, or_14_out);
  and and_61 (and_61_out, not_32_out, Clock);
  and and_62 (and_62_out, Clock, or_15_out);
  and and_63 (and_63_out, not_33_out, Clock);
  and and_64 (and_64_out, Clock, or_16_out);
  nor nor_1 (nor_1_out, and_33_out, nor_2_out);
  nor nor_2 (nor_2_out, nor_1_out, and_34_out);
  nor nor_3 (nor_3_out, and_35_out, nor_4_out);
  nor nor_4 (nor_4_out, nor_3_out, and_36_out);
  nor nor_5 (nor_5_out, and_37_out, nor_6_out);
  nor nor_6 (nor_6_out, nor_5_out, and_38_out);
  nor nor_7 (nor_7_out, and_39_out, nor_8_out);
  nor nor_8 (nor_8_out, nor_7_out, and_40_out);
  nor nor_9 (nor_9_out, and_41_out, nor_10_out);
  nor nor_10 (nor_10_out, nor_9_out, and_42_out);
  nor nor_11 (nor_11_out, and_43_out, nor_12_out);
  nor nor_12 (nor_12_out, nor_11_out, and_44_out);
  nor nor_13 (nor_13_out, and_45_out, nor_14_out);
  nor nor_14 (nor_14_out, nor_13_out, and_46_out);
  nor nor_15 (nor_15_out, and_47_out, nor_16_out);
  nor nor_16 (nor_16_out, nor_15_out, and_48_out);
  nor nor_17 (nor_17_out, and_49_out, nor_18_out);
  nor nor_18 (nor_18_out, nor_17_out, and_50_out);
  nor nor_19 (nor_19_out, and_51_out, nor_20_out);
  nor nor_20 (nor_20_out, nor_19_out, and_52_out);
  nor nor_21 (nor_21_out, and_53_out, nor_22_out);
  nor nor_22 (nor_22_out, nor_21_out, and_54_out);
  nor nor_23 (nor_23_out, and_55_out, nor_24_out);
  nor nor_24 (nor_24_out, nor_23_out, and_56_out);
  nor nor_25 (nor_25_out, and_57_out, nor_26_out);
  nor nor_26 (nor_26_out, nor_25_out, and_58_out);
  nor nor_27 (nor_27_out, and_59_out, nor_28_out);
  nor nor_28 (nor_28_out, nor_27_out, and_60_out);
  nor nor_29 (nor_29_out, and_61_out, nor_30_out);
  nor nor_30 (nor_30_out, nor_29_out, and_62_out);
  nor nor_31 (nor_31_out, and_63_out, nor_32_out);
  nor nor_32 (nor_32_out, nor_31_out, and_64_out);
  not not_35 (not_35_out, nor_1_out);
  and and_65 (and_65_out, not_35_out, not_34_out);
  and and_66 (and_66_out, not_34_out, nor_1_out);
  not not_36 (not_36_out, nor_3_out);
  and and_67 (and_67_out, not_36_out, not_34_out);
  and and_68 (and_68_out, not_34_out, nor_3_out);
  not not_37 (not_37_out, nor_5_out);
  and and_69 (and_69_out, not_37_out, not_34_out);
  and and_70 (and_70_out, not_34_out, nor_5_out);
  not not_38 (not_38_out, nor_7_out);
  and and_71 (and_71_out, not_38_out, not_34_out);
  and and_72 (and_72_out, not_34_out, nor_7_out);
  not not_39 (not_39_out, nor_9_out);
  and and_73 (and_73_out, not_39_out, not_34_out);
  and and_74 (and_74_out, not_34_out, nor_9_out);
  not not_40 (not_40_out, nor_11_out);
  and and_75 (and_75_out, not_40_out, not_34_out);
  and and_76 (and_76_out, not_34_out, nor_11_out);
  not not_41 (not_41_out, nor_13_out);
  and and_77 (and_77_out, not_41_out, not_34_out);
  and and_78 (and_78_out, not_34_out, nor_13_out);
  not not_42 (not_42_out, nor_15_out);
  and and_79 (and_79_out, not_42_out, not_34_out);
  and and_80 (and_80_out, not_34_out, nor_15_out);
  not not_43 (not_43_out, nor_17_out);
  and and_81 (and_81_out, not_43_out, not_34_out);
  and and_82 (and_82_out, not_34_out, nor_17_out);
  not not_44 (not_44_out, nor_19_out);
  and and_83 (and_83_out, not_44_out, not_34_out);
  and and_84 (and_84_out, not_34_out, nor_19_out);
  not not_45 (not_45_out, nor_21_out);
  and and_85 (and_85_out, not_45_out, not_34_out);
  and and_86 (and_86_out, not_34_out, nor_21_out);
  not not_46 (not_46_out, nor_23_out);
  and and_87 (and_87_out, not_46_out, not_34_out);
  and and_88 (and_88_out, not_34_out, nor_23_out);
  not not_47 (not_47_out, nor_25_out);
  and and_89 (and_89_out, not_47_out, not_34_out);
  and and_90 (and_90_out, not_34_out, nor_25_out);
  not not_48 (not_48_out, nor_27_out);
  and and_91 (and_91_out, not_48_out, not_34_out);
  and and_92 (and_92_out, not_34_out, nor_27_out);
  not not_49 (not_49_out, nor_29_out);
  and and_93 (and_93_out, not_49_out, not_34_out);
  and and_94 (and_94_out, not_34_out, nor_29_out);
  not not_50 (not_50_out, nor_31_out);
  and and_95 (and_95_out, not_50_out, not_34_out);
  and and_96 (and_96_out, not_34_out, nor_31_out);
  nor nor_33 (Data_out[0], and_65_out, nor_34_out);
  nor nor_34 (nor_34_out, Data_out[0], and_66_out);
  nor nor_35 (Data_out[1], and_67_out, nor_36_out);
  nor nor_36 (nor_36_out, Data_out[1], and_68_out);
  nor nor_37 (Data_out[2], and_69_out, nor_38_out);
  nor nor_38 (nor_38_out, Data_out[2], and_70_out);
  nor nor_39 (Data_out[3], and_71_out, nor_40_out);
  nor nor_40 (nor_40_out, Data_out[3], and_72_out);
  nor nor_41 (Data_out[4], and_73_out, nor_42_out);
  nor nor_42 (nor_42_out, Data_out[4], and_74_out);
  nor nor_43 (Data_out[5], and_75_out, nor_44_out);
  nor nor_44 (nor_44_out, Data_out[5], and_76_out);
  nor nor_45 (Data_out[6], and_77_out, nor_46_out);
  nor nor_46 (nor_46_out, Data_out[6], and_78_out);
  nor nor_47 (Data_out[7], and_79_out, nor_48_out);
  nor nor_48 (nor_48_out, Data_out[7], and_80_out);
  nor nor_49 (Data_out[8], and_81_out, nor_50_out);
  nor nor_50 (nor_50_out, Data_out[8], and_82_out);
  nor nor_51 (Data_out[9], and_83_out, nor_52_out);
  nor nor_52 (nor_52_out, Data_out[9], and_84_out);
  nor nor_53 (Data_out[10], and_85_out, nor_54_out);
  nor nor_54 (nor_54_out, Data_out[10], and_86_out);
  nor nor_55 (Data_out[11], and_87_out, nor_56_out);
  nor nor_56 (nor_56_out, Data_out[11], and_88_out);
  nor nor_57 (Data_out[12], and_89_out, nor_58_out);
  nor nor_58 (nor_58_out, Data_out[12], and_90_out);
  nor nor_59 (Data_out[13], and_91_out, nor_60_out);
  nor nor_60 (nor_60_out, Data_out[13], and_92_out);
  nor nor_61 (Data_out[14], and_93_out, nor_62_out);
  nor nor_62 (nor_62_out, Data_out[14], and_94_out);
  nor nor_63 (Data_out[15], and_95_out, nor_64_out);
  nor nor_64 (nor_64_out, Data_out[15], and_96_out);
endmodule

module MUX8_1 (
  input  [2:0] rx_sel,
  input  [15:0] rx0,
  input  [15:0] rx1,
  input  [15:0] rx2,
  input  [15:0] rx3,
  input  [15:0] rx4,
  input  [15:0] rx5,
  input  [15:0] rx6,
  input  [15:0] rx7,
  output [15:0] Reading
);

  wire [15:0] and_1_out, and_2_out, and_3_out, and_4_out, and_5_out, and_6_out, and_7_out, and_8_out,
       and_9_out, and_10_out, and_11_out, and_12_out, and_13_out, and_14_out, bit_extender_1_out,
       bit_extender_2_out, bit_extender_3_out, not_1_out, not_2_out, not_3_out, not_4_out, not_5_out,
       not_6_out, not_7_out, or_1_out, or_2_out, or_3_out, or_4_out, or_5_out, or_6_out;

  assign bit_extender_1_out = {{15{rx_sel[0]}}, rx_sel[0]};  // Bit_Extender bit_extender_1
  assign not_1_out = ~bit_extender_1_out;  // NOT_Gate not_1, 16 bits wide
  assign and_1_out = not_1_out & rx0;  // AND_Gate and_1, 16 bits wide
  assign and_2_out = bit_extender_1_out & rx1;  // AND_Gate and_2, 16 bits wide
  assign not_2_out = ~bit_extender_1_out;  // NOT_Gate not_2, 16 bits wide
  assign and_3_out = not_2_out & rx2;  // AND_Gate and_3, 16 bits wide
  assign and_4_out = bit_extender_1_out & rx3;  // AND_Gate and_4, 16 bits wide
  assign not_3_out = ~bit_extender_1_out;  // NOT_Gate not_3, 16 bits wide
  assign and_5_out = not_3_out & rx4;  // AND_Gate and_5, 16 bits wide
  assign and_6_out = bit_extender_1_out & rx5;  // AND_Gate and_6, 16 bits wide
  assign not_4_out = ~bit_extender_1_out;  // NOT_Gate not_4, 16 bits wide
  assign and_7_out = not_4_out & rx6;  // AND_Gate and_7, 16 bits wide
  assign and_8_out = bit_extender_1_out & rx7;  // AND_Gate and_8, 16 bits wide
  assign bit_extender_2_out = {{15{rx_sel[1]}}, rx_sel[1]};  // Bit_Extender bit_extender_2
  assign or_1_out = and_1_out | and_2_out;  // OR_Gate or_1, 16 bits wide
  assign or_2_out = and_3_out | and_4_out;  // OR_Gate or_2, 16 bits wide
  assign or_3_out = and_5_out | and_6_out;  // OR_Gate or_3, 16 bits wide
  assign or_4_out = and_7_out | and_8_out;  // OR_Gate or_4, 16 bits wide
  assign not_5_out = ~bit_extender_2_out;  // NOT_Gate not_5, 16 bits wide
  assign and_9_out = not_5_out & or_1_out;  // AND_Gate and_9, 16 bits wide
  assign and_10_out = bit_extender_2_out & or_2_out;  // AND_Gate and_10, 16 bits wide
  assign not_6_out = ~bit_extender_2_out;  // NOT_Gate not_6, 16 bits wide
  assign and_11_out = not_6_out & or_3_out;  // AND_Gate and_11, 16 bits wide
  assign and_12_out = bit_extender_2_out & or_4_out;  // AND_Gate and_12, 16 bits wide
  assign bit_extender_3_out = {{15{rx_sel[2]}}, rx_sel[2]};  // Bit_Extender bit_extender_3
  assign or_5_out = and_9_out | and_10_out;  // OR_Gate or_5, 16 bits wide
  assign or_6_out = and_11_out | and_12_out;  // OR_Gate or_6, 16 bits wide
  assign not_7_out = ~bit_extender_3_out;  // NOT_Gate not_7, 16 bits wide
  assign and_13_out = not_7_out & or_5_out;  // AND_Gate and_13, 16 bits wide
  assign and_14_out = bit_extender_3_out & or_6_out;  // AND_Gate and_14, 16 bits wide
  assign Reading = and_13_out | and_14_out;  // OR_Gate or_7, 16 bits wide
endmodule

module Core (
  input  in_1,
  input  in_2,
  output [15:0] PCOut
);

  wire alu_1_negativeflag, alu_1_overflowflag, alu_1_zeroflag, clock_1_out, cu_1_buffwrite, cu_1_gprwrite,
       cu_1_irwrite, cu_1_pcwrite, cu_1_ramread, cu_1_ramwrite;
  wire [1:0] cu_1_tobranchornottobranch;
  wire [2:0] and_8_out, and_9_out, cu_1_regmux, cu_1_regmuxsel, not_4_out, or_4_out;
  wire [3:0] cu_1_aluopcode, gprs_1_reg0, gprs_1_reg0_2, gprs_1_reg0_3, gprs_1_reg0_4;
  wire [15:0] alu_1_result, alu_1_resultrx1, and_1_out, and_2_out, and_3_out, and_4_out, and_5_out,
       and_6_out, and_7_out, and_10_out, and_11_out, and_12_out, and_13_out, bit_extender_1_out,
       bit_extender_2_out, bit_extender_3_out, bit_extender_4_out, bit_extender_5_out, bit_extender_6_out,
       bit_extender_7_out, bit_extender_8_out, bit_extender_9_out, cla16bit_1_result, gprs_1_reg1,
       IR_data_out, not_1_out, not_2_out, not_3_out, or_1_out, or_2_out, or_3_out, or_5_out, ram_1_dout,
       reg16bit_1_data_out, rom_1_data;

  assign and_1_out = 16'h1 & not_1_out;  // AND_Gate and_1, 16 bits wide
  assign not_1_out = ~bit_extender_3_out;  // NOT_Gate not_1, 16 bits wide
  assign and_2_out = bit_extender_4_out & bit_extender_3_out;  // AND_Gate and_2, 16 bits wide
  assign or_1_out = and_1_out | and_2_out;  // OR_Gate or_1, 16 bits wide
  ROM #(.addrWidth(16), .dataWidth(16)) rom_1 (.addr(PCOut), .data(rom_1_data));
  CLA16bit cla16bit_1 (.X(PCOut), .Y(or_1_out), .Result(cla16bit_1_result));  // open: isSub, Cin, OverflowFlag
  assign not_2_out = ~bit_extender_7_out;  // NOT_Gate not_2, 16 bits wide
  assign bit_extender_1_out = {{15{in_1}}, in_1};  // Bit_Extender bit_extender_1
  assign and_3_out = PCOut & not_2_out;  // AND_Gate and_3, 16 bits wide
  assign or_2_out = and_3_out | and_4_out;  // OR_Gate or_2, 16 bits wide
  assign and_4_out = cla16bit_1_result & bit_extender_7_out;  // AND_Gate and_4, 16 bits wide
  Clock clock_1 (.out(clock_1_out));
  assign and_5_out = bit_extender_1_out & or_3_out;  // AND_Gate and_5, 16 bits wide
  assign not_3_out = ~bit_extender_2_out;  // NOT_Gate not_3, 16 bits wide
  assign and_6_out = or_2_out & not_3_out;  // AND_Gate and_6, 16 bits wide
  assign or_3_out = and_6_out | and_7_out;  // OR_Gate or_3, 16 bits wide
  assign and_7_out = {gprs_1_reg0_4, gprs_1_reg0_3, gprs_1_reg0_2, gprs_1_reg0} & bit_extender_2_out;  // AND_Gate and_7, 16 bits wide
  assign bit_extender_2_out = {{15{cu_1_tobranchornottobranch[1]}}, cu_1_tobranchornottobranch[1]};  // Bit_Extender bit_extender_2
  assign or_4_out = and_8_out | and_9_out;  // OR_Gate or_4, 3 bits wide
  assign and_8_out = IR_data_out[7:5] & cu_1_regmux;  // AND_Gate and_8, 3 bits wide
  assign and_9_out = IR_data_out[10:8] & not_4_out;  // AND_Gate and_9, 3 bits wide
  Reg16Bit PC (.Data_in(and_5_out), .write_enable(1'b1), .Clock(clock_1_out), .Data_out(PCOut));
  Reg16Bit IR (.Data_in(rom_1_data), .write_enable(cu_1_irwrite), .Clock(clock_1_out), .Data_out(IR_data_out));
  assign not_4_out = ~cu_1_regmux;  // NOT_Gate not_4, 3 bits wide
  assign bit_extender_3_out = {{15{cu_1_tobranchornottobranch[0]}}, cu_1_tobranchornottobranch[0]};  // Bit_Extender bit_extender_3
  assign bit_extender_4_out = {{11{1'b0}}, IR_data_out[4:0]};  // Bit_Extender bit_extender_4
  assign or_5_out = and_10_out | and_11_out | and_12_out | and_13_out;  // OR_Gate or_5, 16 bits wide
  assign and_10_out = reg16bit_1_data_out & bit_extender_9_out;  // AND_Gate and_10, 16 bits wide
  assign and_11_out = bit_extender_6_out & ram_1_dout;  // AND_Gate and_11, 16 bits wide
  assign and_12_out = alu_1_result & bit_extender_8_out;  // AND_Gate and_12, 16 bits wide
  assign and_13_out = bit_extender_4_out & bit_extender_5_out;  // AND_Gate and_13, 16 bits wide
  assign bit_extender_5_out = {{15{cu_1_regmuxsel[2]}}, cu_1_regmuxsel[2]};  // Bit_Extender bit_extender_5
  GPRs gprs_1 (
    .RegWrite_enable(cu_1_gprwrite), .regW(or_4_out), .Data_In(or_5_out), .Clock(clock_1_out),
    .reg0_idx(IR_data_out[10:8]), .reg1_idx(IR_data_out[7:5]),
    .reg0({gprs_1_reg0_4, gprs_1_reg0_3, gprs_1_reg0_2, gprs_1_reg0}), .reg1(gprs_1_reg1));
  CU cu_1 (
    .IROpcode(IR_data_out[15:11]), .Clock(clock_1_out), .Reset(in_2), .ZeroFlag(alu_1_zeroflag),
    .OverflowFlag(alu_1_overflowflag), .NegativeFlag(alu_1_negativeflag), .regMuxSel(cu_1_regmuxsel),
    .IRWrite(cu_1_irwrite), .PCWrite(cu_1_pcwrite), .ALUOpcode(cu_1_aluopcode), .GPRWrite(cu_1_gprwrite),
    .RAMWrite(cu_1_ramwrite), .RAMRead(cu_1_ramread), .ToBranchOrNotToBranch(cu_1_tobranchornottobranch),
    .RegMux(cu_1_regmux), .BuffWrite(cu_1_buffwrite));
  assign bit_extender_6_out = {{15{cu_1_regmuxsel[1]}}, cu_1_regmuxsel[1]};  // Bit_Extender bit_extender_6
  assign bit_extender_7_out = {{15{cu_1_pcwrite}}, cu_1_pcwrite};  // Bit_Extender bit_extender_7
  assign bit_extender_8_out = {{15{cu_1_regmuxsel[0]}}, cu_1_regmuxsel[0]};  // Bit_Extender bit_extender_8
  RAM #(.addrWidth(16), .dataWidth(16)) ram_1 (
    .addr(gprs_1_reg1), .we(cu_1_ramwrite), .oe(cu_1_ramread), .clk(clock_1_out),
    .din({gprs_1_reg0_4, gprs_1_reg0_3, gprs_1_reg0_2, gprs_1_reg0}), .dout(ram_1_dout));
  assign bit_extender_9_out = {{13{cu_1_regmux[2]}}, cu_1_regmux};  // Bit_Extender bit_extender_9
  ALU alu_1 (
    .X({gprs_1_reg0_4, gprs_1_reg0_3, gprs_1_reg0_2, gprs_1_reg0}), .Y(gprs_1_reg1), .opcode(cu_1_aluopcode),
    .Shift(IR_data_out[4:0]), .Result(alu_1_result), .OverflowFlag(alu_1_overflowflag),
    .ZeroFlag(alu_1_zeroflag), .NegativeFlag(alu_1_negativeflag), .ResultRx1(alu_1_resultrx1));
  Hex_Digit_Display #(.decimalPoint("false")) hex_digit_display_1 (.value(gprs_1_reg0_4));
  Hex_Digit_Display #(.decimalPoint("false")) hex_digit_display_2 (.value(gprs_1_reg0_3));
  Reg16Bit reg16bit_1 (
    .Data_in(alu_1_resultrx1), .write_enable(cu_1_buffwrite), .Clock(clock_1_out),
    .Data_out(reg16bit_1_data_out));
  Hex_Digit_Display #(.decimalPoint("false")) hex_digit_display_3 (.value(gprs_1_reg0_2));
  Hex_Digit_Display #(.decimalPoint("false")) hex_digit_display_4 (.value(gprs_1_reg0));

  // Notes on the sheet:
  //   contents of rom_1 (hex, n*v repeats v):
  //   9000 9101 931f 941f 7b80 1200 1220 1020 1140 1a40 e065
endmodule

module CU (
  input  [4:0] IROpcode,
  input  Clock,
  input  Reset,
  input  ZeroFlag,
  input  OverflowFlag,
  input  NegativeFlag,
  output [2:0] regMuxSel,
  output IRWrite,
  output PCWrite,
  output [3:0] ALUOpcode,
  output GPRWrite,
  output RAMWrite,
  output RAMRead,
  output [1:0] ToBranchOrNotToBranch,
  output [2:0] RegMux,
  output BuffWrite
);

  wire and_1_out, and_2_out, and_3_out, and_4_out, and_7_out, and_8_out, and_9_out, and_10_out, and_11_out,
       and_17_out, and_18_out, and_19_out, and_23_out, and_24_out, and_25_out, and_26_out, and_27_out,
       and_28_out, and_29_out, and_30_out, and_31_out, and_32_out, and_33_out, and_34_out, and_35_out,
       and_36_out, and_37_out, and_38_out, and_39_out, and_40_out, and_41_out, and_42_out, and_43_out,
       and_44_out, and_45_out, and_46_out, and_47_out, and_48_out, and_49_out, and_50_out, and_51_out,
       and_52_out, and_53_out, and_54_out, and_55_out, and_56_out, nor_1_out, nor_2_out, nor_3_out,
       nor_4_out, nor_5_out, nor_6_out, nor_7_out, nor_8_out, nor_9_out, nor_10_out, nor_11_out, nor_12_out,
       nor_13_out, nor_14_out, nor_15_out, nor_16_out, nor_17_out, nor_18_out, nor_19_out, nor_20_out,
       not_1_out, not_2_out, not_3_out, not_4_out, not_5_out, not_6_out, not_7_out, not_8_out, not_9_out,
       not_10_out, not_11_out, not_12_out, not_13_out, not_14_out, not_15_out, not_16_out, not_17_out,
       not_18_out, not_20_out, not_21_out, not_22_out, not_23_out, not_24_out, not_25_out, not_26_out,
       not_27_out, not_28_out, not_29_out, not_30_out, not_31_out, not_32_out, not_33_out, not_34_out,
       not_35_out, or_1_out, or_3_out, or_4_out, or_6_out, or_7_out, or_8_out, or_10_out, xor_1_out;
  wire [1:0] bit_extender_3_out, or_2_out;
  wire [3:0] and_15_out, and_20_out, and_21_out, bit_extender_1_out, bit_extender_2_out, not_19_out;

  and and_1 (and_1_out, IROpcode[4], IROpcode[0]);
  and and_2 (and_2_out, IROpcode[1], IROpcode[4]);
  and and_3 (and_3_out, IROpcode[2], IROpcode[4]);
  and and_4 (and_4_out, IROpcode[3], IROpcode[4]);
  not not_1 (not_1_out, and_1_out);
  and and_5 (regMuxSel[2], not_1_out, and_2_out, not_2_out, not_3_out);
  not not_2 (not_2_out, and_3_out);
  not not_3 (not_3_out, and_4_out);
  not not_4 (not_4_out, and_1_out);
  not not_5 (not_5_out, and_2_out);
  and and_6 (regMuxSel[1], not_4_out, not_5_out, and_3_out, not_6_out);
  not not_6 (not_6_out, and_4_out);
  not not_7 (not_7_out, and_1_out);
  and and_7 (and_7_out, not_7_out, and_2_out, and_3_out, not_8_out);
  not not_8 (not_8_out, and_4_out);
  and and_8 (and_8_out, and_1_out, and_2_out, and_3_out, and_4_out);
  not not_9 (not_9_out, and_1_out);
  and and_9 (and_9_out, not_9_out, and_2_out, and_3_out, and_4_out);
  not not_10 (not_10_out, and_1_out);
  not not_11 (not_11_out, and_2_out);
  and and_10 (and_10_out, not_10_out, not_11_out, and_3_out, and_4_out);
  not not_12 (not_12_out, and_1_out);
  not not_13 (not_13_out, and_2_out);
  and and_11 (and_11_out, not_12_out, not_13_out, not_14_out, and_4_out);
  not not_14 (not_14_out, and_3_out);
  not not_15 (not_15_out, and_2_out);
  and and_12 (or_2_out[1], and_1_out, not_15_out, not_16_out, not_17_out);
  not not_16 (not_16_out, and_3_out);
  not not_17 (not_17_out, and_4_out);
  not not_18 (not_18_out, IROpcode[4]);
  and and_13 (regMuxSel[0], not_18_out, not_22_out);
  or or_1 (or_1_out, and_8_out, and_9_out, and_10_out, and_11_out);
  assign ToBranchOrNotToBranch = or_2_out & bit_extender_3_out;  // AND_Gate and_14, 2 bits wide
  assign bit_extender_1_out = {{3{IROpcode[4]}}, IROpcode[4]};  // Bit_Extender bit_extender_1
  assign and_15_out = bit_extender_1_out & bit_extender_2_out;  // AND_Gate and_15, 4 bits wide
  and and_16 (RAMWrite, and_7_out, nor_17_out);
  assign bit_extender_2_out = {{3{or_1_out}}, or_1_out};  // Bit_Extender bit_extender_2
  and and_17 (and_17_out, and_8_out, ZeroFlag);
  and and_18 (and_18_out, and_9_out, not_20_out);
  or or_2 (or_2_out[0], and_17_out, and_18_out, and_23_out, and_24_out);
  or or_3 (or_3_out, or_2_out[0], or_2_out[1]);
  and and_19 (and_19_out, IROpcode[3], IROpcode[2], IROpcode[1], IROpcode[0]);
  assign and_20_out = IROpcode[3:0] & not_19_out;  // AND_Gate and_20, 4 bits wide
  assign not_19_out = ~and_15_out;  // NOT_Gate not_19, 4 bits wide
  assign and_21_out = 4'b0100 & and_15_out;  // AND_Gate and_21, 4 bits wide
  and and_22 (RAMRead, regMuxSel[1], nor_17_out);
  or or_4 (or_4_out, or_1_out, or_2_out[1]);
  not not_20 (not_20_out, ZeroFlag);
  not not_21 (not_21_out, NegativeFlag);
  xor xor_1 (xor_1_out, OverflowFlag, NegativeFlag);
  and and_23 (and_23_out, and_10_out, xor_1_out);
  and and_24 (and_24_out, and_11_out, and_26_out);
  assign bit_extender_3_out = {{1{and_51_out}}, and_51_out};  // Bit_Extender bit_extender_3
  not not_22 (not_22_out, and_25_out);
  and and_25 (and_25_out, nor_15_out, and_19_out);
  assign ALUOpcode = and_20_out | and_21_out;  // OR_Gate or_5, 4 bits wide
  not not_23 (not_23_out, ZeroFlag);
  and and_26 (and_26_out, not_21_out, not_23_out);
  and and_27 (and_27_out, or_4_out, nor_15_out);
  and and_28 (and_28_out, regMuxSel[2], nor_15_out);
  or or_6 (or_6_out, and_27_out, and_28_out, and_29_out, and_30_out);
  and and_29 (and_29_out, and_7_out, nor_19_out);
  and and_30 (and_30_out, nor_17_out, regMuxSel[0]);
  not not_24 (not_24_out, IRWrite);
  and and_31 (and_31_out, not_24_out, Clock);
  and and_32 (and_32_out, Clock, IRWrite);
  not not_25 (not_25_out, nor_11_out);
  and and_33 (and_33_out, not_25_out, Clock);
  and and_34 (and_34_out, Clock, nor_11_out);
  not not_26 (not_26_out, nor_13_out);
  and and_35 (and_35_out, not_26_out, Clock);
  and and_36 (and_36_out, Clock, nor_13_out);
  not not_27 (not_27_out, nor_15_out);
  and and_37 (and_37_out, not_27_out, Clock);
  and and_38 (and_38_out, Clock, nor_15_out);
  not not_28 (not_28_out, nor_17_out);
  and and_39 (and_39_out, not_28_out, Clock);
  and and_40 (and_40_out, Clock, nor_17_out);
  not not_29 (not_29_out, Clock);
  or or_7 (or_7_out, Reset, or_6_out);
  not not_30 (not_30_out, nor_1_out);
  nor nor_1 (nor_1_out, and_31_out, or_7_out, nor_2_out);
  nor nor_2 (nor_2_out, nor_1_out, and_32_out);
  not not_31 (not_31_out, nor_3_out);
  nor nor_3 (nor_3_out, and_33_out, or_7_out, nor_4_out);
  nor nor_4 (nor_4_out, nor_3_out, and_34_out);
  not not_32 (not_32_out, nor_5_out);
  nor nor_5 (nor_5_out, and_35_out, or_7_out, nor_6_out);
  nor nor_6 (nor_6_out, nor_5_out, and_36_out);
  not not_33 (not_33_out, nor_7_out);
  nor nor_7 (nor_7_out, and_37_out, or_7_out, nor_8_out);
  nor nor_8 (nor_8_out, nor_7_out, and_38_out);
  not not_34 (not_34_out, nor_9_out);
  nor nor_9 (nor_9_out, and_39_out, or_7_out, nor_10_out);
  nor nor_10 (nor_10_out, nor_9_out, and_40_out);
  and and_41 (and_41_out, not_30_out, not_29_out);
  and and_42 (and_42_out, not_29_out, nor_1_out);
  and and_43 (and_43_out, not_31_out, not_29_out);
  and and_44 (and_44_out, not_29_out, nor_3_out);
  and and_45 (and_45_out, not_32_out, not_29_out);
  and and_46 (and_46_out, not_29_out, nor_5_out);
  and and_47 (and_47_out, not_33_out, not_29_out);
  and and_48 (and_48_out, not_29_out, nor_7_out);
  and and_49 (and_49_out, not_34_out, not_29_out);
  and and_50 (and_50_out, not_29_out, nor_9_out);
  nor nor_11 (nor_11_out, and_41_out, nor_12_out);
  nor nor_12 (nor_12_out, nor_11_out, and_42_out);
  nor nor_13 (nor_13_out, and_43_out, nor_14_out);
  nor nor_14 (nor_14_out, nor_13_out, and_44_out);
  nor nor_15 (nor_15_out, and_45_out, nor_16_out);
  nor nor_16 (nor_16_out, nor_15_out, and_46_out);
  nor nor_17 (nor_17_out, and_47_out, nor_18_out);
  nor nor_18 (nor_18_out, nor_17_out, and_48_out);
  nor nor_19 (nor_19_out, and_49_out, nor_20_out);
  nor nor_20 (nor_20_out, nor_19_out, and_50_out);
  nor nor_21 (IRWrite, nor_11_out, nor_13_out, nor_15_out, nor_17_out, nor_19_out);
  and and_51 (and_51_out, nor_13_out, or_3_out);
  or or_8 (or_8_out, nor_15_out, nor_13_out);
  not not_35 (not_35_out, and_19_out);
  or or_9 (PCWrite, IRWrite, and_51_out);
  and and_52 (and_52_out, or_8_out, and_19_out);
  and and_53 (and_53_out, nor_13_out, regMuxSel[2]);
  and and_54 (and_54_out, regMuxSel[0], not_35_out, nor_15_out);
  and and_55 (and_55_out, nor_19_out, regMuxSel[1]);
  or or_10 (or_10_out, and_54_out, and_55_out);
  and and_56 (and_56_out, nor_15_out, and_19_out);
  assign RegMux = {{2{and_56_out}}, and_56_out};  // Bit_Extender bit_extender_4
  or or_11 (GPRWrite, and_53_out, and_52_out, or_10_out);
  and and_57 (BuffWrite, and_19_out, nor_13_out);
endmodule

module WT4bit (
  input  [3:0] X,
  input  [3:0] Y,
  output [15:0] O
);

  wire and_2_out, and_5_out, and_6_out, and_7_out, and_8_out, and_9_out, and_10_out, and_11_out, and_12_out,
       and_13_out, and_14_out, and_15_out, and_16_out, and_17_out, and_18_out, and_19_out, and_20_out,
       and_21_out, and_22_out, and_23_out, and_24_out, and_25_out, and_26_out, and_27_out, and_28_out,
       and_29_out, or_1_out, or_2_out, or_3_out, or_4_out, xor_1_out, xor_2_out, xor_3_out, xor_5_out,
       xor_7_out, xor_9_out;
  wire [4:1] and_4_out;
  wire [7:0] and_1_out;

  and and_1 (and_1_out[0], X[0], Y[0]);
  and and_2 (and_2_out, X[3], Y[3]);
  and and_3 (and_1_out[1], X[0], Y[1]);
  and and_4 (and_4_out[1], X[1], Y[0]);
  and and_5 (and_5_out, X[0], Y[2]);
  and and_6 (and_6_out, X[1], Y[1]);
  and and_7 (and_7_out, X[2], Y[0]);
  and and_8 (and_8_out, X[1], Y[3]);
  and and_9 (and_9_out, X[2], Y[2]);
  and and_10 (and_10_out, X[3], Y[1]);
  and and_11 (and_11_out, X[2], Y[3]);
  and and_12 (and_12_out, X[3], Y[2]);
  xor xor_1 (xor_1_out, and_5_out, and_6_out);
  and and_13 (and_13_out, X[0], Y[3]);
  and and_14 (and_14_out, X[1], Y[2]);
  and and_15 (and_15_out, X[2], Y[1]);
  and and_16 (and_16_out, X[3], Y[0]);
  xor xor_2 (xor_2_out, and_8_out, and_9_out);
  xor xor_3 (xor_3_out, and_11_out, and_12_out);
  xor xor_4 (and_1_out[2], xor_1_out, and_7_out);
  and and_17 (and_17_out, xor_1_out, and_7_out);
  or or_1 (or_1_out, and_17_out, and_18_out);
  and and_18 (and_18_out, and_6_out, and_5_out);
  xor xor_5 (xor_5_out, and_13_out, and_14_out);
  xor xor_6 (and_1_out[4], xor_2_out, and_10_out);
  and and_19 (and_19_out, xor_2_out, and_10_out);
  and and_20 (and_20_out, and_9_out, and_8_out);
  xor xor_7 (xor_7_out, xor_3_out, or_4_out);
  and and_21 (and_21_out, xor_3_out, or_4_out);
  or or_2 (or_2_out, and_21_out, and_22_out);
  and and_22 (and_22_out, and_12_out, and_11_out);
  xor xor_8 (and_1_out[3], xor_5_out, and_15_out);
  and and_23 (and_23_out, xor_5_out, and_15_out);
  or or_3 (or_3_out, and_23_out, and_24_out);
  and and_24 (and_24_out, and_14_out, and_13_out);
  or or_4 (or_4_out, and_19_out, and_20_out);
  xor xor_9 (xor_9_out, or_2_out, and_2_out);
  xor xor_10 (and_4_out[3], and_16_out, or_1_out);
  and and_25 (and_25_out, or_1_out, and_16_out);
  xor xor_11 (and_4_out[4], and_25_out, or_3_out);
  and and_26 (and_26_out, and_25_out, or_3_out);
  and and_27 (and_27_out, and_26_out, xor_7_out);
  xor xor_12 (and_1_out[6], xor_9_out, and_27_out);
  and and_28 (and_28_out, xor_9_out, and_27_out);
  and and_29 (and_29_out, and_2_out, or_2_out);
  xor xor_13 (and_1_out[5], and_26_out, xor_7_out);
  or or_5 (and_1_out[7], and_28_out, and_29_out);
  CLA16bit cla16bit_1 (
    .X({{8{1'b0}}, and_1_out}), .Y({{11{1'b0}}, and_4_out[4:3], 1'b0, and_4_out[1], 1'b0}), .isSub(1'b0),
    .Result(O));  // open: Cin, OverflowFlag
endmodule

module WT16bit (
  input  [15:0] X,
  input  [15:0] Y,
  output [31:0] out_3
);

  wire cla16bit_14_overflowflag, cla16bit_16_overflowflag;
  wire [15:0] cla16bit_1_result, cla16bit_2_result, cla16bit_3_result, cla16bit_4_result, cla16bit_5_result,
       cla16bit_6_result, cla16bit_7_result, cla16bit_8_result, cla16bit_9_result, cla16bit_10_result,
       cla16bit_11_result, cla16bit_12_result, cla16bit_13_result, cla16bit_14_result, cla16bit_15_result,
       wt4bit_1_o, wt4bit_2_o, wt4bit_3_o, wt4bit_4_o, wt4bit_5_o, wt4bit_6_o, wt4bit_7_o, wt4bit_8_o,
       wt4bit_9_o, wt4bit_10_o, wt4bit_11_o, wt4bit_12_o, wt4bit_13_o, wt4bit_14_o, wt4bit_15_o, wt4bit_16_o;
  wire [31:0] bit_extender_1_out, bit_extender_2_out, bit_extender_3_out;

  WT4bit wt4bit_1 (.X(X[3:0]), .Y(Y[3:0]), .O(wt4bit_1_o));
  WT4bit wt4bit_2 (.X(X[3:0]), .Y(Y[7:4]), .O(wt4bit_2_o));
  WT4bit wt4bit_3 (.X(X[7:4]), .Y(Y[3:0]), .O(wt4bit_3_o));
  WT4bit wt4bit_4 (.X(X[3:0]), .Y(Y[11:8]), .O(wt4bit_4_o));
  WT4bit wt4bit_5 (.X(X[7:4]), .Y(Y[7:4]), .O(wt4bit_5_o));
  WT4bit wt4bit_6 (.X(X[11:8]), .Y(Y[3:0]), .O(wt4bit_6_o));
  WT4bit wt4bit_7 (.X(X[3:0]), .Y(Y[15:12]), .O(wt4bit_7_o));
  WT4bit wt4bit_8 (.X(X[7:4]), .Y(Y[11:8]), .O(wt4bit_8_o));
  WT4bit wt4bit_9 (.X(X[11:8]), .Y(Y[7:4]), .O(wt4bit_9_o));
  WT4bit wt4bit_10 (.X(X[15:12]), .Y(Y[3:0]), .O(wt4bit_10_o));
  WT4bit wt4bit_11 (.X(X[7:4]), .Y(Y[15:12]), .O(wt4bit_11_o));
  WT4bit wt4bit_12 (.X(X[11:8]), .Y(Y[11:8]), .O(wt4bit_12_o));
  WT4bit wt4bit_13 (.X(X[15:12]), .Y(Y[7:4]), .O(wt4bit_13_o));
  WT4bit wt4bit_14 (.X(X[11:8]), .Y(Y[15:12]), .O(wt4bit_14_o));
  WT4bit wt4bit_15 (.X(X[15:12]), .Y(Y[11:8]), .O(wt4bit_15_o));
  WT4bit wt4bit_16 (.X(X[15:12]), .Y(Y[15:12]), .O(wt4bit_16_o));
  CLA16bit cla16bit_1 (
    .X(wt4bit_1_o), .Y({wt4bit_2_o[11:0], 4'b0000}), .Result(cla16bit_1_result));  // open: isSub, Cin, OverflowFlag
  CLA16bit cla16bit_2 (
    .X({wt4bit_3_o[11:0], 4'b0000}), .Y({wt4bit_4_o[7:0], {8{1'b0}}}), .Result(cla16bit_2_result));  // open: isSub, Cin, OverflowFlag
  CLA16bit cla16bit_3 (
    .X({wt4bit_5_o[7:0], {8{1'b0}}}), .Y({wt4bit_6_o[7:0], {8{1'b0}}}), .Result(cla16bit_3_result));  // open: isSub, Cin, OverflowFlag
  CLA16bit cla16bit_4 (
    .X({wt4bit_7_o[11:0], 4'b0000}), .Y({wt4bit_8_o[11:0], 4'b0000}), .Result(cla16bit_4_result));  // open: isSub, Cin, OverflowFlag
  CLA16bit cla16bit_5 (
    .X({wt4bit_9_o[11:0], 4'b0000}), .Y({wt4bit_10_o[11:0], 4'b0000}), .Result(cla16bit_5_result));  // open: isSub, Cin, OverflowFlag
  CLA16bit cla16bit_6 (.X(wt4bit_12_o), .Y(wt4bit_13_o), .Result(cla16bit_6_result));  // open: isSub, Cin, OverflowFlag
  CLA16bit cla16bit_7 (
    .X({wt4bit_14_o[11:0], 4'b0000}), .Y({wt4bit_15_o[11:0], 4'b0000}), .Result(cla16bit_7_result));  // open: isSub, Cin, OverflowFlag
  CLA16bit cla16bit_8 (
    .X(cla16bit_1_result), .Y(cla16bit_2_result), .Result(cla16bit_8_result));  // open: isSub, Cin, OverflowFlag
  CLA16bit cla16bit_9 (
    .X(cla16bit_4_result), .Y(cla16bit_5_result), .Result(cla16bit_9_result));  // open: isSub, Cin, OverflowFlag
  assign bit_extender_1_out = {{16{1'b0}}, cla16bit_10_result};  // Bit_Extender bit_extender_1
  CLA16bit cla16bit_10 (
    .X(cla16bit_8_result), .Y(cla16bit_3_result), .Result(cla16bit_10_result));  // open: isSub, Cin, OverflowFlag
  CLA16bit cla16bit_11 (
    .X(cla16bit_6_result), .Y(cla16bit_7_result), .Result(cla16bit_11_result));  // open: isSub, Cin, OverflowFlag
  assign bit_extender_2_out = {{16{1'b0}}, cla16bit_12_result};  // Bit_Extender bit_extender_2
  CLA16bit cla16bit_12 (
    .X(cla16bit_9_result), .Y({wt4bit_11_o[11:0], 4'b0000}), .Result(cla16bit_12_result));  // open: isSub, Cin, OverflowFlag
  CLA16bit cla16bit_13 (
    .X(cla16bit_11_result), .Y({wt4bit_16_o[7:0], {8{1'b0}}}), .Result(cla16bit_13_result));  // open: isSub, Cin, OverflowFlag
  assign bit_extender_3_out = {{16{1'b0}}, cla16bit_13_result};  // Bit_Extender bit_extender_3
  CLA16bit cla16bit_14 (
    .X(bit_extender_1_out[15:0]), .Y({bit_extender_2_out[7:0], {8{1'b0}}}), .Result(cla16bit_14_result),
    .OverflowFlag(cla16bit_14_overflowflag));  // open: isSub, Cin
  CLA16bit cla16bit_15 (
    .X(bit_extender_1_out[31:16]), .Y(bit_extender_2_out[23:8]), .Cin(cla16bit_14_overflowflag),
    .Result(cla16bit_15_result));  // open: isSub, OverflowFlag
  CLA16bit cla16bit_16 (
    .X({16{1'b0}}), .Y(cla16bit_14_result), .Result(out_3[15:0]), .OverflowFlag(cla16bit_16_overflowflag));  // open: isSub, Cin
  CLA16bit cla16bit_17 (
    .X(bit_extender_3_out[15:0]), .Y(cla16bit_15_result), .Cin(cla16bit_16_overflowflag),
    .Result(out_3[31:16]));  // open: isSub, OverflowFlag
endmodule
