// Logisim project adder.circ as structural Verilog: 1 circuit, main circuit main
module main (
  input  [15:0] in_1,
  input  [15:0] in_2,
  input  in_3,
  input  in_4,
  output [15:0] out_5
);

  wire and_1_out, and_2_out, and_3_out, and_4_out, and_5_out, and_6_out, and_7_out, and_8_out, and_9_out,
       and_10_out, and_11_out, and_12_out, and_13_out, and_14_out, and_15_out, and_16_out, and_17_out,
       and_18_out, and_19_out, and_20_out, and_21_out, and_22_out, and_23_out, and_24_out, and_25_out,
       and_26_out, and_27_out, and_28_out, and_29_out, and_30_out, and_31_out, and_32_out, or_1_out,
       or_2_out, or_3_out, or_4_out, or_5_out, or_6_out, or_7_out, or_8_out, or_9_out, or_10_out, or_11_out,
       or_12_out, or_13_out, or_14_out, or_15_out, or_16_out, xor_1_out, xor_2_out, xor_3_out, xor_4_out,
       xor_9_out, xor_10_out, xor_11_out, xor_12_out, xor_17_out, xor_18_out, xor_19_out, xor_20_out,
       xor_25_out, xor_26_out, xor_27_out, xor_28_out;

  xor xor_1 (xor_1_out, in_1[0], in_2[0]);
  xor xor_2 (xor_2_out, in_1[4], in_2[4]);
  xor xor_3 (xor_3_out, in_1[8], in_2[8]);
  xor xor_4 (xor_4_out, in_1[12], in_2[12]);
  and and_1 (and_1_out, xor_1_out, in_3);
  and and_2 (and_2_out, in_1[0], in_2[0]);
  xor xor_5 (out_5[0], xor_1_out, in_3);
  xor xor_6 (out_5[4], xor_2_out, or_13_out);
  and and_3 (and_3_out, xor_2_out, or_13_out);
  and and_4 (and_4_out, in_1[4], in_2[4]);
  xor xor_7 (out_5[8], xor_3_out, or_14_out);
  and and_5 (and_5_out, xor_3_out, or_14_out);
  and and_6 (and_6_out, in_1[8], in_2[8]);
  xor xor_8 (out_5[12], xor_4_out, or_15_out);
  and and_7 (and_7_out, xor_4_out, or_15_out);
  and and_8 (and_8_out, in_1[12], in_2[12]);
  or or_1 (or_1_out, and_1_out, and_2_out);
  or or_2 (or_2_out, and_3_out, and_4_out);
  or or_3 (or_3_out, and_5_out, and_6_out);
  or or_4 (or_4_out, and_7_out, and_8_out);
  xor xor_9 (xor_9_out, in_1[1], in_2[1]);
  xor xor_10 (xor_10_out, in_1[5], in_2[5]);
  xor xor_11 (xor_11_out, in_1[9], in_2[9]);
  xor xor_12 (xor_12_out, in_1[13], in_2[13]);
  xor xor_13 (out_5[1], xor_9_out, or_1_out);
  and and_9 (and_9_out, xor_9_out, or_1_out);
  and and_10 (and_10_out, in_1[1], in_2[1]);
  xor xor_14 (out_5[5], xor_10_out, or_2_out);
  and and_11 (and_11_out, xor_10_out, or_2_out);
  and and_12 (and_12_out, in_1[5], in_2[5]);
  xor xor_15 (out_5[9], xor_11_out, or_3_out);
  and and_13 (and_13_out, xor_11_out, or_3_out);
  and and_14 (and_14_out, in_1[9], in_2[9]);
  xor xor_16 (out_5[13], xor_12_out, or_4_out);
  and and_15 (and_15_out, xor_12_out, or_4_out);
  and and_16 (and_16_out, in_1[13], in_2[13]);
  or or_5 (or_5_out, and_9_out, and_10_out);
  or or_6 (or_6_out, and_11_out, and_12_out);
  or or_7 (or_7_out, and_13_out, and_14_out);
  or or_8 (or_8_out, and_15_out, and_16_out);
  xor xor_17 (xor_17_out, in_1[2], in_2[2]);
  xor xor_18 (xor_18_out, in_1[6], in_2[6]);
  xor xor_19 (xor_19_out, in_1[10], in_2[10]);
  xor xor_20 (xor_20_out, in_1[14], in_2[14]);
  xor xor_21 (out_5[2], xor_17_out, or_5_out);
  and and_17 (and_17_out, xor_17_out, or_5_out);
  and and_18 (and_18_out, in_1[2], in_2[2]);
  and and_19 (and_19_out, xor_18_out, or_6_out);
  and and_20 (and_20_out, in_1[6], in_2[6]);
  and and_21 (and_21_out, xor_19_out, or_7_out);
  and and_22 (and_22_out, in_1[10], in_2[10]);
  and and_23 (and_23_out, xor_20_out, or_8_out);
  and and_24 (and_24_out, in_1[14], in_2[14]);
  xor xor_22 (out_5[6], xor_18_out, or_6_out);
  xor xor_23 (out_5[10], xor_19_out, or_7_out);
  xor xor_24 (out_5[14], xor_20_out, or_8_out);
  or or_9 (or_9_out, and_17_out, and_18_out);
  or or_10 (or_10_out, and_19_out, and_20_out);
  or or_11 (or_11_out, and_21_out, and_22_out);
  or or_12 (or_12_out, and_23_out, and_24_out);
  xor xor_25 (xor_25_out, in_1[3], in_2[3]);
  xor xor_26 (xor_26_out, in_1[7], in_2[7]);
  xor xor_27 (xor_27_out, in_1[11], in_2[11]);
  xor xor_28 (xor_28_out, in_1[0], in_2[15]);
  xor xor_29 (out_5[3], xor_25_out, or_9_out);
  and and_25 (and_25_out, xor_25_out, or_9_out);
  and and_26 (and_26_out, in_1[3], in_2[3]);
  xor xor_30 (out_5[7], xor_26_out, or_10_out);
  and and_27 (and_27_out, xor_26_out, or_10_out);
  and and_28 (and_28_out, in_1[7], in_2[7]);
  xor xor_31 (out_5[11], xor_27_out, or_11_out);
  and and_29 (and_29_out, xor_27_out, or_11_out);
  and and_30 (and_30_out, in_1[11], in_2[11]);
  xor xor_32 (out_5[15], xor_28_out, or_12_out);
  and and_31 (and_31_out, xor_28_out, or_12_out);
  and and_32 (and_32_out, in_1[0], in_2[15]);
  or or_13 (or_13_out, and_25_out, and_26_out);
  or or_14 (or_14_out, and_27_out, and_28_out);
  or or_15 (or_15_out, and_29_out, and_30_out);
  or or_16 (or_16_out, and_31_out, and_32_out);
endmodule
